// Digital circuit 32位计算机.dig as structural Verilog
module \_32位计算机  (
  input  Clock,
  output [31:0] KSP,
  output [3:0] STATE,
  output [7:0] IR,
  output [31:0] PC,
  output [31:0] KFP,
  output [31:0] USP,
  output [31:0] UFP
);

  wire add_1_c_o, and_4_out, and_6_out, and_7_out, and_8_out, and_9_out, and_11_out, and_12_out, and_13_out,
       and_14_out, and_15_out, and_16_out, and_17_out, and_18_out, and_19_out, and_20_out, and_21_out,
       and_22_out, and_23_out, and_24_out, AV_IInstERR, AV_Keyboard, AV_MEMERR, AV_Telnet, AV_Timer, clock_t,
       CLR_IE, CLR_KernelMode, comparator_2_eq, comparator_3_eq, comparator_4_eq, CS_IVT, CS_KeyBoard,
       CS_RAM, CS_ROM, CS_Stack, CS_Telnet, CS_Terminal, CS_Timer, CS_URAM, CS_UROM, CS_UStack,
       decoder_1_out_0, decoder_1_out_1, delay_1_out, delay_2_out, delay_3_out, delay_4_out, delay_5_out,
       DN_SP, driverinvsel_1_out, EN_KSP, EN_USP, END_CYCLE, Flag_c, Flag_n, Flag_v, Flag_v_Bus, Flag_z,
       HALT, HALT_eq, INC_PC, INT_REQ, INT_RET, INT_TAKE, Kernel_Mode, Kernel_Use_USP, KernelMode_Bus, LD_FP,
       LD_IR, LD_KFP, LD_KSP, LD_MAR, LD_MDREXT, LD_MDRINT, LD_PC, LD_RFlags, LD_Rflags_Bus, LD_Rw, LD_SP,
       LD_UFP, LD_USP, multiplexer_4_out, multiplexer_9_out, multiplexer_11_out, multiplexer_12_out,
       multiplexer_13_out, multiplexer_14_out, multiplexer_15_out, multiplexer_16_out, not_1_out, not_2_out,
       not_3_out, not_4_out, not_5_out, not_6_out, not_7_out, not_9_out, not_10_out, not_11_out, not_12_out,
       not_13_out, not_14_out, not_15_out, not_17_out, not_18_out, not_19_out, not_20_out, not_21_out,
       nPSR_q, OE, OE_ALU, OE_FP, OE_INT_REQ, OE_KFP, OE_KSP, OE_MDREXT, OE_MDRINT, OE_PC, OE_Ra, OE_Rb,
       OE_Rflags, OE_SP, OE_UFP, OE_USP, or_1_out, or_6_out, or_7_out, or_8_out, or_9_out, or_10_out,
       or_11_out, or_12_out, or_13_out, or_14_out, or_15_out, R_IE_q, SET_IE, SET_KernelMode, Sign_A, Sign_B,
       Sign_R, SignedCalc, sub_1_c_o, Timer_ovf, UP_SP, Update_Kernel_Mode_Stable, Use_USP, WE, xnor_2_out,
       xor_1_out, xor_3_out, xor_4_out, xor_5_out, xor_6_out;
  wire [2:0] priorityencoder_1_num;
  wire [3:0] ADDR_Ra, ADDR_Rb, ADDR_Rw, MODE_ALU;
  wire [5:0] RegFile_db;
  wire [6:6] RegFile_db_2;
  wire [7:0] telnet_1_out;
  wire [15:0] keyboard_1_d;
  wire [30:0] multiplexer_10_out, RegFile_da;
  wire [30:7] RegFile_db_3;
  wire [31:0] add_1_s, and_5_out, Dec_s, Div_S_q, Div_S_r, Div_U_q, Div_U_r, driver_1_out, driver_12_out,
       Inc_s, INT_ADDR, MAR_q, MDR_EXT_q, MDR_INT_q, multiplexer_5_out, multiplexer_7_out, multiplexer_8_out,
       nand_1_out, nor_1_out, not_8_out, or_5_out, Shift_S_out, Shift_U_out, sub_1_s, xnor_1_out, xor_2_out;
  wire [31:20] IR_q;
  wire [32:23] multiplexer_3_out;
  wire [34:0] CU_K_d, multiplexer_1_out, multiplexer_2_out;
  wire [35:0] CU_U_d;
  wire [36:0] CU_INT_d;
  wire [63:0] Mul_S_mul, Mul_U_mul, multiplexer_6_out;

  assign {driver_1_out[31:5], KernelMode_Bus, Flag_v_Bus, driver_1_out[2:0]} = OE_INT_REQ ? INT_ADDR : 32'bz;  // Driver driver_1
  CounterPreset #(.maxValue(15), .Bits(4)) u_STATE (
    .en(1'b1), .C(clock_t), .dir(1'b0), .in(4'b0000), .ld(1'b0), .clr(END_CYCLE), .out(STATE));  // open: ovf
  Register #(.Bits(32)) u_IR (
    .D({driver_1_out[31:5], KernelMode_Bus, Flag_v_Bus, driver_1_out[2:0]}), .C(clock_t), .en(LD_IR),
    .Q({IR_q, ADDR_Ra, ADDR_Rb, ADDR_Rw, IR}));
  assign {driver_1_out[31:5], KernelMode_Bus, Flag_v_Bus, driver_1_out[2:0]} = OE_PC ? PC : 32'bz;  // Driver driver_2
  assign {driver_1_out[31:5], KernelMode_Bus, Flag_v_Bus, driver_1_out[2:0]} = OE_Rflags ? {{27{1'b0}}, Kernel_Mode, Flag_v, Flag_n, Flag_c, Flag_z} : 32'bz;  // Driver driver_3
  Comparator #(.Bits(8)) u_HALT (.a(IR), .b(8'hf0), .eq(HALT_eq));  // open: gt, lt
  and and_1 (HALT, Kernel_Mode, HALT_eq);
  assign {driver_1_out[31:5], KernelMode_Bus, Flag_v_Bus, driver_1_out[2:0]} = OE_Ra ? {Sign_A, RegFile_da} : 32'bz;  // Driver driver_4
  RegisterFile #(.AddrBits(4), .Bits(32)) RegFile (
    .Din({driver_1_out[31:5], KernelMode_Bus, Flag_v_Bus, driver_1_out[2:0]}), .we(LD_Rw), .Rw(ADDR_Rw),
    .C(clock_t), .Ra(ADDR_Ra), .Rb(ADDR_Rb), .Da({Sign_A, RegFile_da}),
    .Db({Sign_B, RegFile_db_3, RegFile_db_2[6], RegFile_db}));
  assign {driver_1_out[31:5], KernelMode_Bus, Flag_v_Bus, driver_1_out[2:0]} = OE_Rb ? {Sign_B, RegFile_db_3, RegFile_db_2[6], RegFile_db} : 32'bz;  // Driver driver_5
  CounterPreset #(.Bits(32)) u_KSP (
    .en(EN_KSP), .C(clock_t), .dir(DN_SP),
    .in({driver_1_out[31:5], KernelMode_Bus, Flag_v_Bus, driver_1_out[2:0]}), .ld(LD_KSP), .clr(1'b0),
    .out(KSP));  // open: ovf
  assign {driver_1_out[31:5], KernelMode_Bus, Flag_v_Bus, driver_1_out[2:0]} = OE_KSP ? KSP : 32'bz;  // Driver driver_6
  CounterPreset #(.Bits(32)) u_USP (
    .en(EN_USP), .C(clock_t), .dir(DN_SP),
    .in({driver_1_out[31:5], KernelMode_Bus, Flag_v_Bus, driver_1_out[2:0]}), .ld(LD_USP), .clr(1'b0),
    .out(USP));  // open: ovf
  assign {driver_1_out[31:5], KernelMode_Bus, Flag_v_Bus, driver_1_out[2:0]} = OE_USP ? USP : 32'bz;  // Driver driver_7
  Register #(.Bits(32)) u_KFP (
    .D({driver_1_out[31:5], KernelMode_Bus, Flag_v_Bus, driver_1_out[2:0]}), .C(clock_t), .en(LD_KFP), .Q(KFP));
  assign {driver_1_out[31:5], KernelMode_Bus, Flag_v_Bus, driver_1_out[2:0]} = OE_KFP ? KFP : 32'bz;  // Driver driver_8
  Register #(.Bits(32)) u_UFP (
    .D({driver_1_out[31:5], KernelMode_Bus, Flag_v_Bus, driver_1_out[2:0]}), .C(clock_t), .en(LD_UFP), .Q(UFP));
  assign {driver_1_out[31:5], KernelMode_Bus, Flag_v_Bus, driver_1_out[2:0]} = OE_UFP ? UFP : 32'bz;  // Driver driver_9
  Comparator #(.Bits(4)) comparator_1 (.a(STATE), .b(4'b0010), .eq(Update_Kernel_Mode_Stable));  // open: gt, lt
  CounterPreset #(.Bits(32), .isProgramCounter("true")) u_PC (
    .en(INC_PC), .C(clock_t), .dir(1'b0),
    .in({driver_1_out[31:5], KernelMode_Bus, Flag_v_Bus, driver_1_out[2:0]}), .ld(LD_PC), .clr(1'b0), .out(PC));  // open: ovf
  ROM #(.AddrBits(4), .Bits(37)) CU_INT (.A(STATE), .sel(INT_TAKE), .D(CU_INT_d));
  ROM #(.AddrBits(12), .isProgramMemory("true"), .Bits(36)) CU_U (.A({IR, STATE}), .sel(1'b1), .D(CU_U_d));
  ROM #(.AddrBits(12), .isProgramMemory("true"), .Bits(36)) CU_K (
    .A({IR, STATE}), .sel(1'b1), .D({Kernel_Use_USP, CU_K_d}));
  or or_1 (or_1_out, UP_SP, DN_SP);
  Comparator #(.Bits(8)) comparator_2 (.a(IR), .b(8'h33), .eq(comparator_2_eq));  // open: gt, lt
  Multiplexer #(.Bits(37)) multiplexer_1 (
    .sel(INT_TAKE), .in_0({37{1'b0}}), .in_1(CU_INT_d), .out({INT_RET, OE_INT_REQ, multiplexer_1_out}));
  and and_2 (AV_IInstERR, not_1_out, CU_U_d[35]);
  not not_1 (not_1_out, Kernel_Mode);
  Multiplexer #(.Bits(35)) multiplexer_2 (
    .sel(Kernel_Mode), .in_0(CU_U_d[34:0]), .in_1(CU_K_d), .out(multiplexer_2_out));
  assign {driver_1_out[31:5], KernelMode_Bus, Flag_v_Bus, driver_1_out[2:0]} = OE_ALU ? {Sign_R, multiplexer_10_out} : 32'bz;  // Driver driver_10
  Demultiplexer demultiplexer_1 (.sel(Use_USP), .in(OE_SP), .out_0(OE_KSP), .out_1(OE_USP));
  Demultiplexer demultiplexer_2 (.sel(Use_USP), .in(LD_SP), .out_0(LD_KSP), .out_1(LD_USP));
  Demultiplexer demultiplexer_3 (.sel(Use_USP), .in(or_1_out), .out_0(EN_KSP), .out_1(EN_USP));
  Demultiplexer demultiplexer_4 (.sel(Use_USP), .in(OE_FP), .out_0(OE_KFP), .out_1(OE_UFP));
  Demultiplexer demultiplexer_5 (.sel(Use_USP), .in(LD_FP), .out_0(LD_KFP), .out_1(LD_UFP));
  assign driverinvsel_1_out = ~comparator_2_eq ? and_7_out : 1'bz;  // DriverInvSel driverinvsel_1
  or or_2 (INC_PC, multiplexer_3_out[23], driverinvsel_1_out);
  not not_2 (not_2_out, Flag_z);
  Multiplexer #(.Bits(35)) multiplexer_3 (
    .sel(INT_TAKE), .in_0(multiplexer_2_out), .in_1(multiplexer_1_out),
    .out({SET_KernelMode, CLR_KernelMode, multiplexer_3_out[32:31], SignedCalc, MODE_ALU, WE, OE, multiplexer_3_out[23], SET_IE, CLR_IE, OE_ALU, OE_Rflags, OE_Rb, OE_Ra, OE_MDREXT, OE_MDRINT, OE_PC, OE_SP, OE_FP, LD_Rflags_Bus, LD_RFlags, LD_Rw, LD_IR, LD_MDREXT, LD_MDRINT, LD_MAR, LD_PC, LD_SP, LD_FP, UP_SP, DN_SP}));
  and and_3 (clock_t, Clock, not_3_out);
  not not_3 (not_3_out, HALT);
  or or_3 (Use_USP, Kernel_Use_USP, not_4_out);
  not not_4 (not_4_out, Kernel_Mode);
  or or_4 (END_CYCLE, and_7_out, multiplexer_3_out[32]);
  not not_5 (not_5_out, Flag_c);
  not not_6 (not_6_out, Flag_z);
  xor xor_1 (xor_1_out, Flag_n, Flag_v);
  and and_4 (and_4_out, not_2_out, not_7_out);
  not not_7 (not_7_out, xor_1_out);
  Add #(.Bits(32)) add_1 (
    .a({Sign_A, RegFile_da}), .b({Sign_B, RegFile_db_3, RegFile_db_2[6], RegFile_db}), .c_i(1'b0),
    .s(add_1_s), .c_o(add_1_c_o));
  Sub #(.Bits(32)) sub_1 (
    .a({Sign_A, RegFile_da}), .b({Sign_B, RegFile_db_3, RegFile_db_2[6], RegFile_db}), .c_i(1'b0),
    .s(sub_1_s), .c_o(sub_1_c_o));
  BarrelShifter #(.Bits(32)) Shift_U (.in({Sign_A, RegFile_da}), .shift(RegFile_db), .out(Shift_U_out));
  assign and_5_out = {Sign_A, RegFile_da} & {Sign_B, RegFile_db_3, RegFile_db_2[6], RegFile_db};  // And and_5, 32 bits wide
  assign nand_1_out = ~({Sign_A, RegFile_da} & {Sign_B, RegFile_db_3, RegFile_db_2[6], RegFile_db});  // NAnd nand_1, 32 bits wide
  assign or_5_out = {Sign_A, RegFile_da} | {Sign_B, RegFile_db_3, RegFile_db_2[6], RegFile_db};  // Or or_5, 32 bits wide
  assign nor_1_out = ~({Sign_A, RegFile_da} | {Sign_B, RegFile_db_3, RegFile_db_2[6], RegFile_db});  // NOr nor_1, 32 bits wide
  assign xor_2_out = {Sign_A, RegFile_da} ^ {Sign_B, RegFile_db_3, RegFile_db_2[6], RegFile_db};  // XOr xor_2, 32 bits wide
  assign xnor_1_out = ~({Sign_A, RegFile_da} ^ {Sign_B, RegFile_db_3, RegFile_db_2[6], RegFile_db});  // XNOr xnor_1, 32 bits wide
  assign not_8_out = ~{Sign_A, RegFile_da};  // Not not_8, 32 bits wide
  Add #(.Bits(32)) Inc (.a({Sign_A, RegFile_da}), .b(32'h1), .c_i(1'b0), .s(Inc_s));  // open: c_o
  Sub #(.Bits(32)) Dec (.a({Sign_A, RegFile_da}), .b(32'h1), .c_i(1'b0), .s(Dec_s));  // open: c_o
  and and_6 (and_6_out, not_5_out, not_6_out);
  Multiplexer #(.Selector_Bits(4)) multiplexer_4 (
    .sel(IR_q[23:20]), .in_0(1'b0), .in_1(Flag_c), .in_2(Flag_z), .in_3(and_6_out), .in_4(not_9_out),
    .in_5(not_10_out), .in_6(not_11_out), .in_7(Flag_n), .in_8(Flag_v), .in_9(xor_1_out), .in_10(not_12_out),
    .in_11(and_4_out), .in_12(not_13_out), .in_13(1'b0), .in_14(1'b0), .in_15(1'b0), .out(multiplexer_4_out));
  not not_9 (not_9_out, Flag_c);
  not not_10 (not_10_out, Flag_z);
  not not_11 (not_11_out, and_6_out);
  not not_12 (not_12_out, xor_1_out);
  not not_13 (not_13_out, and_4_out);
  BarrelShifter #(.Bits(32), .barrelShifterMode("arithmetic"), .barrelSigned("true")) Shift_S (
    .in({Sign_A, RegFile_da}), .shift({RegFile_db_2[6], RegFile_db}), .out(Shift_S_out));
  and and_7 (and_7_out, multiplexer_3_out[31], not_14_out);
  not not_14 (not_14_out, multiplexer_4_out);
  Mul #(.Bits(32)) Mul_U (
    .a({Sign_A, RegFile_da}), .b({Sign_B, RegFile_db_3, RegFile_db_2[6], RegFile_db}), .mul(Mul_U_mul));
  Mul #(.Signed("true"), .Bits(32)) Mul_S (
    .a({Sign_A, RegFile_da}), .b({Sign_B, RegFile_db_3, RegFile_db_2[6], RegFile_db}), .mul(Mul_S_mul));
  Div #(.Bits(32)) Div_U (
    .a({Sign_A, RegFile_da}), .b({Sign_B, RegFile_db_3, RegFile_db_2[6], RegFile_db}), .q(Div_U_q),
    .r(Div_U_r));
  Div #(.remainderPositive("false"), .Signed("true"), .Bits(32)) Div_S (
    .a({Sign_A, RegFile_da}), .b({Sign_B, RegFile_db_3, RegFile_db_2[6], RegFile_db}), .q(Div_S_q),
    .r(Div_S_r));
  Multiplexer #(.Bits(32)) multiplexer_5 (
    .sel(SignedCalc), .in_0(Shift_U_out), .in_1(Shift_S_out), .out(multiplexer_5_out));
  RS_FF R_IE (.S(SET_IE), .C(clock_t), .R(CLR_IE), .Q(R_IE_q));  // open: nQ
  xor xor_3 (xor_3_out, SET_KernelMode, CLR_KernelMode);
  Multiplexer #(.Bits(64)) multiplexer_6 (
    .sel(SignedCalc), .in_0(Mul_U_mul), .in_1(Mul_S_mul), .out(multiplexer_6_out));
  not not_15 (not_15_out, KernelMode_Bus);
  or or_6 (or_6_out, xor_3_out, LD_Rflags_Bus);
  Multiplexer #(.Bits(32)) multiplexer_7 (.sel(SignedCalc), .in_0(Div_U_q), .in_1(Div_S_q), .out(multiplexer_7_out));
  Multiplexer #(.Bits(32)) multiplexer_8 (.sel(SignedCalc), .in_0(Div_U_r), .in_1(Div_S_r), .out(multiplexer_8_out));
  and and_8 (and_8_out, END_CYCLE, INT_REQ, R_IE_q);
  Multiplexer multiplexer_9 (.sel(LD_Rflags_Bus), .in_0(CLR_KernelMode), .in_1(not_15_out), .out(multiplexer_9_out));
  Register nPSR (.D(multiplexer_9_out), .C(clock_t), .en(or_6_out), .Q(nPSR_q));
  not not_16 (Kernel_Mode, nPSR_q);
  Register #(.Bits(32)) MAR (
    .D({driver_1_out[31:5], KernelMode_Bus, Flag_v_Bus, driver_1_out[2:0]}), .C(clock_t), .en(LD_MAR),
    .Q(MAR_q));
  RS_FF rs_ff_1 (.S(and_8_out), .C(clock_t), .R(INT_RET), .Q(INT_TAKE));  // open: nQ
  Decoder decoder_1 (.sel(MAR_q[27]), .out_0(decoder_1_out_0), .out_1(decoder_1_out_1));
  assign {driver_1_out[31:5], KernelMode_Bus, Flag_v_Bus, driver_1_out[2:0]} = OE_MDRINT ? MDR_INT_q : 32'bz;  // Driver driver_11
  Register #(.Bits(32)) MDR_EXT (
    .D({driver_1_out[31:5], KernelMode_Bus, Flag_v_Bus, driver_1_out[2:0]}), .C(clock_t), .en(LD_MDREXT),
    .Q(MDR_EXT_q));
  Multiplexer #(.Selector_Bits(4), .Bits(32)) multiplexer_10 (
    .sel(MODE_ALU), .in_0(add_1_s), .in_1(sub_1_s), .in_2(multiplexer_6_out[31:0]), .in_3(multiplexer_7_out),
    .in_4(multiplexer_5_out), .in_5(and_5_out), .in_6(nand_1_out), .in_7(or_5_out), .in_8(nor_1_out),
    .in_9(xor_2_out), .in_10(xnor_1_out), .in_11(not_8_out), .in_12(Inc_s), .in_13(Dec_s),
    .in_14(multiplexer_8_out), .in_15({32{1'b0}}), .out({Sign_R, multiplexer_10_out}));
  xnor xnor_2 (xnor_2_out, Sign_A, Sign_B);
  xor xor_4 (xor_4_out, Sign_A, Sign_B);
  not not_17 (not_17_out, Kernel_Mode);
  and and_9 (and_9_out, decoder_1_out_0, Kernel_Mode);
  Register #(.Bits(32)) MDR_INT (.D(driver_12_out), .C(clock_t), .en(LD_MDRINT), .Q(MDR_INT_q));
  assign driver_12_out = OE_MDREXT ? MDR_EXT_q : 32'bz;  // Driver driver_12
  xor xor_5 (xor_5_out, Sign_A, Sign_R);
  xor xor_6 (xor_6_out, Sign_A, Sign_R);
  and and_10 (AV_MEMERR, decoder_1_out_0, not_17_out);
  Demultiplexer #(.Selector_Bits(3)) demultiplexer_6 (
    .sel(MAR_q[26:24]), .in(and_9_out), .out_0(CS_ROM), .out_1(CS_RAM), .out_2(CS_Stack), .out_3(CS_IVT),
    .out_4(CS_KeyBoard), .out_5(CS_Terminal), .out_6(CS_Telnet), .out_7(CS_Timer));
  Demultiplexer #(.Selector_Bits(3)) demultiplexer_7 (
    .sel(MAR_q[26:24]), .in(decoder_1_out_1), .out_0(CS_UROM), .out_1(CS_URAM), .out_2(CS_UStack));  // open: out_3, out_4, out_5, out_6, out_7
  Comparator #(.Bits(4)) comparator_3 (.a(MODE_ALU), .b(4'b0001), .eq(comparator_3_eq));  // open: gt, lt
  and and_11 (and_11_out, xnor_2_out, xor_5_out);
  and and_12 (and_12_out, xor_4_out, xor_6_out);
  Comparator #(.Bits(32)) comparator_4 (
    .a({32{1'b0}}), .b({Sign_R, multiplexer_10_out}), .eq(comparator_4_eq));  // open: gt, lt
  Multiplexer multiplexer_11 (
    .sel(not_19_out), .in_0(driver_1_out[1]), .in_1(multiplexer_12_out), .out(multiplexer_11_out));
  Multiplexer multiplexer_12 (.sel(comparator_3_eq), .in_0(add_1_c_o), .in_1(sub_1_c_o), .out(multiplexer_12_out));
  Multiplexer multiplexer_13 (.sel(comparator_3_eq), .in_0(and_11_out), .in_1(and_12_out), .out(multiplexer_13_out));
  not not_18 (not_18_out, LD_Rflags_Bus);
  Multiplexer multiplexer_14 (
    .sel(not_18_out), .in_0(driver_1_out[0]), .in_1(comparator_4_eq), .out(multiplexer_14_out));
  not not_19 (not_19_out, LD_Rflags_Bus);
  Multiplexer multiplexer_15 (.sel(not_20_out), .in_0(driver_1_out[2]), .in_1(Sign_R), .out(multiplexer_15_out));
  not not_20 (not_20_out, LD_Rflags_Bus);
  Multiplexer multiplexer_16 (.sel(not_21_out), .in_0(Flag_v_Bus), .in_1(multiplexer_13_out), .out(multiplexer_16_out));
  or or_7 (or_7_out, LD_Rflags_Bus, LD_RFlags);
  not not_21 (not_21_out, LD_Rflags_Bus);
  or or_8 (or_8_out, LD_Rflags_Bus, LD_RFlags);
  or or_9 (or_9_out, LD_Rflags_Bus, LD_RFlags);
  or or_10 (or_10_out, LD_Rflags_Bus, LD_RFlags);
  Register register_1 (.D(multiplexer_16_out), .C(clock_t), .en(or_7_out), .Q(Flag_v));
  Register register_2 (.D(multiplexer_14_out), .C(clock_t), .en(or_8_out), .Q(Flag_z));
  Register register_3 (.D(multiplexer_11_out), .C(clock_t), .en(or_9_out), .Q(Flag_c));
  Register register_4 (.D(multiplexer_15_out), .C(clock_t), .en(or_10_out), .Q(Flag_n));
  PriorityEncoder #(.Selector_Bits(3)) priorityencoder_1 (
    .in0(1'b0), .in1(AV_Telnet), .in2(AV_Keyboard), .in3(1'b0), .in4(AV_Timer), .in5(1'b0),
    .in6(AV_IInstERR), .in7(AV_MEMERR), .num(priorityencoder_1_num), .any(INT_REQ));
  Multiplexer #(.Selector_Bits(3), .Bits(32)) multiplexer_17 (
    .sel(priorityencoder_1_num), .in_0(32'h3000003), .in_1(32'h3000002), .in_2(32'h3000001),
    .in_3(32'h3000000), .in_4(32'h3000007), .in_5(32'h3000006), .in_6(32'h3000005), .in_7(32'h3000004),
    .out(INT_ADDR));
  or or_11 (or_11_out, WE, OE);
  and and_13 (and_13_out, CS_KeyBoard, OE);
  and and_14 (and_14_out, CS_Terminal, WE);
  and and_15 (and_15_out, CS_Telnet, WE);
  and and_16 (and_16_out, CS_Telnet, OE);
  EEPROM #(.AddrBits(24), .Bits(32)) ROM (.A(MAR_q[23:0]), .CS(CS_ROM), .WE(1'b0), .OE(OE), .D(driver_12_out));
  RAMSinglePortSel #(.AddrBits(24), .Bits(32)) RAM (
    .A(MAR_q[23:0]), .CS(delay_1_out), .WE(WE), .OE(OE), .D(driver_12_out));
  Delay delay_1 (.in(and_17_out), .out(delay_1_out));
  and and_17 (and_17_out, CS_RAM, or_12_out);
  or or_12 (or_12_out, WE, OE);
  RAMSinglePortSel #(.AddrBits(24), .Bits(32)) Stack (
    .A(MAR_q[23:0]), .CS(delay_2_out), .WE(WE), .OE(OE), .D(driver_12_out));
  Delay delay_2 (.in(and_18_out), .out(delay_2_out));
  and and_18 (and_18_out, CS_Stack, or_13_out);
  or or_13 (or_13_out, WE, OE);
  RAMSinglePortSel #(.AddrBits(24), .Bits(32)) IVT (
    .A(MAR_q[23:0]), .CS(delay_3_out), .WE(WE), .OE(OE), .D(driver_12_out));
  Delay delay_3 (.in(and_19_out), .out(delay_3_out));
  and and_19 (and_19_out, CS_IVT, or_11_out);
  Keyboard keyboard_1 (.C(clock_t), .en(and_13_out), .D(keyboard_1_d), .av(AV_Keyboard));
  Terminal terminal_1 (.D(driver_12_out[15:0]), .C(clock_t), .en(and_14_out));
  Telnet #(.port(8081)) telnet_1 (
    .in(driver_12_out[7:0]), .C(clock_t), .wr(and_15_out), .rd(and_16_out), .out(telnet_1_out), .av(AV_Telnet));
  Counter #(.Bits(13)) Timer (.en(1'b1), .C(clock_t), .clr(CS_Timer), .ovf(Timer_ovf));  // open: out
  EEPROM #(.AddrBits(24), .Bits(32)) UROM (.A(MAR_q[23:0]), .CS(CS_UROM), .WE(1'b0), .OE(OE), .D(driver_12_out));
  RAMSinglePortSel #(.AddrBits(24), .Bits(32)) URAM (
    .A(MAR_q[23:0]), .CS(delay_4_out), .WE(WE), .OE(OE), .D(driver_12_out));
  Delay delay_4 (.in(and_20_out), .out(delay_4_out));
  and and_20 (and_20_out, CS_URAM, or_14_out);
  or or_14 (or_14_out, WE, OE);
  RAMSinglePortSel #(.AddrBits(24), .Bits(32)) UStack (
    .A(MAR_q[23:0]), .CS(delay_5_out), .WE(WE), .OE(OE), .D(driver_12_out));
  Delay delay_5 (.in(and_21_out), .out(delay_5_out));
  and and_21 (and_21_out, CS_UStack, or_15_out);
  or or_15 (or_15_out, WE, OE);
  and and_22 (and_22_out, CS_Timer, OE);
  and and_23 (and_23_out, CS_KeyBoard, OE);
  assign driver_12_out = and_23_out ? {{16{1'b0}}, keyboard_1_d} : 32'bz;  // Driver driver_13
  assign driver_12_out = and_24_out ? {{24{1'b0}}, telnet_1_out} : 32'bz;  // Driver driver_14
  assign driver_12_out = and_22_out ? 32'h1 : 32'bz;  // Driver driver_15
  RS_FF_AS rs_ff_as_1 (.S(Timer_ovf), .R(CS_Timer), .Q(AV_Timer));  // open: nQ
  and and_24 (and_24_out, CS_Telnet, OE);

  // Notes on the sheet:
  //   Clock: Hz: 655
  //   contents of CU_INT (hex, n*v repeats v):
  //   3c280080,43c000000,3c002020,3e010002,3c002020,3c004080,3e010002
  //   ,83c000020,3d000040,113c008010
  //   contents of CU_U (hex, n*v repeats v):
  //   3c004020,3d800040,3c008100,13c000000,12*3c000000,3c004020,3d800040
  //   ,3c008100,13c000000,12*3c000000,3c004020,3d800040,3c008100,13c000000
  //   ,12*3c000000,3c004020,3d800040,3c008100,13c000000,12*3c000000
  //   ,3c004020,3d800040,3c008100,13c000000,12*3c000000,3c004020,3d800040
  //   ,3c008100,13c000000,12*3c000000,3c004020,3d800040,3c008100,13c000000
  //   ,12*3c000000,3c004020,3d800040,3c008100,13c000000,12*3c000000
  //   ,3c004020,3d800040,3c008100,13c000000,12*3c000000,3c004020,3d800040
  //   ,3c008100,13c000000,12*3c000000,3c004020,3d800040,3c008100,13c000000
  //   ,12*3c000000,3c004020,3d800040,3c008100,13c000000,12*3c000000
  //   ,3c004020,3d800040,3c008100,13c000000,12*3c000000,3c004020,3d800040
  //   ,3c008100,13c000000,12*3c000000,3c004020,3d800040,3c008100,13c000000
  //   ,12*3c000000,3c004020,3d800040,3c008100,13c000000,12*3c000000
  //   ,3c004020,3d800040,3c008100,13c020200,12*3c000000,3c004020,3d800040
  //   ,3c008100,3c040020,3d000040,13c008200,10*3c000000,3c004020,3d800040
  //   ,3c008100,3c040020,3c020080,13e010000,10*3c000000,3c004020,3d800040
  //   ,3c008100,3c004020,3d800040,3c008020,3d000040,13c008200,8*3c000000
  //   ,3c004020,3d800040,3c008100,3c004020,3d800040,3c008020,3c020080
  //   ,13e010000,8*3c000000,3c004020,3d800040,3c008100,3c804020,3d000040
  //   ,13c008200,10*3c000000,3c004020,3d800040,3c008100,3c804020,3d000040
  //   ,13c008200,10*3c000000,3c004020,3d800040,3c008100,100020,3d000040
  //   ,13c008200,10*3c000000,3c004020,3d800040,3c008100,13c000000,12*3c000000
  //   ,3c004020,3d800040,3c008100,13c000000,12*3c000000,3c004020,3d800040
  //   ,3c008100,13c000000,12*3c000000,3c004020,3d800040,3c008100,13c000000
  //   ,12*3c000000,3c004020,3d800040,3c008100,13c000000,12*3c000000
  //   ,3c004020,3d800040,3c008100,13c000000,12*3c000000,3c004020,3d800040
  //   ,3c008100,13c000000,12*3c000000,3c004020,3d800040,3c008100,13c000000
  //   ,12*3c000000,3c004020,3d800040,3c008100,100100600,12*3c000000
  //   ,3c004020,3d800040,3c008100,104100600,12*3c000000,3c004020,3d800040
  //   ,3c008100,130100200,12*3c000000,3c004020,3d800040,3c008100,134100200
  //   ,12*3c000000,3c004020,3d800040,3c008100,108100600,12*3c000000
  //   ,3c004020,3d800040,3c008100,10c100600,12*3c000000,3c004020,3d800040
  //   ,3c008100,138100600,12*3c000000,3c004020,3d800040,3c008100,110100600
  //   ,12*3c000000,3c004020,3d800040,3c008100,114100600,12*3c000000
  //   ,3c004020,3d800040,3c008100,118100600,12*3c000000,3c004020,3d800040
  //   ,3c008100,11c100600,12*3c000000,3c004020,3d800040,3c008100,120100600
  //   ,12*3c000000,3c004020,3d800040,3c008100,124100600,12*3c000000
  //   ,3c004020,3d800040,3c008100,128100600,12*3c000000,3c004020,3d800040
  //   ,3c008100,12c100600,12*3c000000,3c004020,3d800040,3c008100,104000400
  //   ,12*3c000000,3c004020,3d800040,3c008100,3c004020,3d800040,13c008010
  //   ,10*3c000000,3c004020,3d800040,3c008100,80000000,3c004020,3d800040
  //   ,13c008010,9*3c000000,3c004020,3d800040,3c008100,13c020010,12*3c000000
  //   ,3c004020,3d800040,3c008100,80000000,13c020010,11*3c000000,3c004020
  //   ,3d800040,3c008100,3c804020,3d000040,3c002020,3c004080,3e010002
  //   ,13c008010,7*3c000000,3c004020,3d800040,3c008100,80000000,3c804020
  //   ,3d000040,3c002020,3c004080,3e010002,13c008010,6*3c000000,3c004020
  //   ,3d800040,3c008100,3c000001,3c002020,3d000040,13c008010,9*3c000000
  //   ,3c004020,3d800040,3c008100,3ca04020,3d000040,3c080080,43c000000
  //   ,3c002020,3e010002,3c002020,3c004080,3e010002,13c008010,3c000000,3c000000,3c000000
  //   ,3c004020,3d800040,3c008100,bc000000,3ca04020,3d000040,3c080080
  //   ,43c000000,3c002020,3e010002,3c002020,3c004080,3e010002,13c008010
  //   ,3c000000,3c000000,3c004020,3d800040,3c008100,93c000000,12*3c000000
  //   ,3c004020,3d800040,3c008100,93c000000,12*3c000000,3c004020,3d800040
  //   ,3c008100,93c000000,12*3c000000,3c004020,3d800040,3c008100,13c000000
  //   ,12*3c000000,3c004020,3d800040,3c008100,13c000000,12*3c000000
  //   ,3c004020,3d800040,3c008100,13c000000,12*3c000000,3c004020,3d800040
  //   ,3c008100,13c000000,12*3c000000,3c004020,3d800040,3c008100,3c002020
  //   ,3c020080,13e010002,10*3c000000,3c004020,3d800040,3c008100,3c000001
  //   ,3c002020,3d000040,13c008200,9*3c000000,3c004020,3d800040,3c008100
  //   ,13c020008,12*3c000000,3c004020,3d800040,3c008100,13c002200,12*3c000000
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  //   contents of CU_K (hex, n*v repeats v):
  //   3c004020,3d800040,3c008100,13c000000,12*3c000000,3c004020,3d800040
  //   ,3c008100,13c000000,12*3c000000,3c004020,3d800040,3c008100,13c000000
  //   ,12*3c000000,3c004020,3d800040,3c008100,13c000000,12*3c000000
  //   ,3c004020,3d800040,3c008100,13c000000,12*3c000000,3c004020,3d800040
  //   ,3c008100,13c000000,12*3c000000,3c004020,3d800040,3c008100,13c000000
  //   ,12*3c000000,3c004020,3d800040,3c008100,13c000000,12*3c000000
  //   ,3c004020,3d800040,3c008100,13c000000,12*3c000000,3c004020,3d800040
  //   ,3c008100,13c000000,12*3c000000,3c004020,3d800040,3c008100,13c000000
  //   ,12*3c000000,3c004020,3d800040,3c008100,13c000000,12*3c000000
  //   ,3c004020,3d800040,3c008100,13c000000,12*3c000000,3c004020,3d800040
  //   ,3c008100,13c000000,12*3c000000,3c004020,3d800040,3c008100,13c000000
  //   ,12*3c000000,3c004020,3d800040,3c008100,13c000000,12*3c000000
  //   ,3c004020,3d800040,3c008100,13c020200,12*3c000000,3c004020,3d800040
  //   ,3c008100,3c040020,3d000040,13c008200,10*3c000000,3c004020,3d800040
  //   ,3c008100,3c040020,3c020080,13e010000,10*3c000000,3c004020,3d800040
  //   ,3c008100,3c004020,3d800040,3c008020,3d000040,13c008200,8*3c000000
  //   ,3c004020,3d800040,3c008100,3c004020,3d800040,3c008020,3c020080
  //   ,13e010000,8*3c000000,3c004020,3d800040,3c008100,3c804020,3d000040
  //   ,13c008200,10*3c000000,3c004020,3d800040,3c008100,3c804020,3d000040
  //   ,13c008200,10*3c000000,3c004020,3d800040,3c008100,100020,3d000040
  //   ,13c008200,10*3c000000,3c004020,3d800040,3c008100,13c000000,12*3c000000
  //   ,3c004020,3d800040,3c008100,13c000000,12*3c000000,3c004020,3d800040
  //   ,3c008100,13c000000,12*3c000000,3c004020,3d800040,3c008100,13c000000
  //   ,12*3c000000,3c004020,3d800040,3c008100,13c000000,12*3c000000
  //   ,3c004020,3d800040,3c008100,13c000000,12*3c000000,3c004020,3d800040
  //   ,3c008100,13c000000,12*3c000000,3c004020,3d800040,3c008100,13c000000
  //   ,12*3c000000,3c004020,3d800040,3c008100,100100600,12*3c000000
  //   ,3c004020,3d800040,3c008100,104100600,12*3c000000,3c004020,3d800040
  //   ,3c008100,130100200,12*3c000000,3c004020,3d800040,3c008100,134100200
  //   ,12*3c000000,3c004020,3d800040,3c008100,108100600,12*3c000000
  //   ,3c004020,3d800040,3c008100,10c100600,12*3c000000,3c004020,3d800040
  //   ,3c008100,138100600,12*3c000000,3c004020,3d800040,3c008100,110100600
  //   ,12*3c000000,3c004020,3d800040,3c008100,114100600,12*3c000000
  //   ,3c004020,3d800040,3c008100,118100600,12*3c000000,3c004020,3d800040
  //   ,3c008100,11c100600,12*3c000000,3c004020,3d800040,3c008100,120100600
  //   ,12*3c000000,3c004020,3d800040,3c008100,124100600,12*3c000000
  //   ,3c004020,3d800040,3c008100,128100600,12*3c000000,3c004020,3d800040
  //   ,3c008100,12c100600,12*3c000000,3c004020,3d800040,3c008100,104000400
  //   ,12*3c000000,3c004020,3d800040,3c008100,3c004020,3d800040,13c008010
  //   ,10*3c000000,3c004020,3d800040,3c008100,80000000,3c004020,3d800040
  //   ,13c008010,9*3c000000,3c004020,3d800040,3c008100,13c020010,12*3c000000
  //   ,3c004020,3d800040,3c008100,80000000,13c020010,11*3c000000,3c004020
  //   ,3d800040,3c008100,3c804020,3d000040,3c002020,3c004080,3e010002
  //   ,13c008010,7*3c000000,3c004020,3d800040,3c008100,80000000,3c804020
  //   ,3d000040,3c002020,3c004080,3e010002,13c008010,6*3c000000,3c004020
  //   ,3d800040,3c008100,3c000001,3c002020,3d000040,13c008010,9*3c000000
  //   ,3c004020,3d800040,3c008100,3ca04020,3d000040,3c080080,43c000000
  //   ,3c002020,3e010002,3c002020,3c004080,3e010002,13c008010,3c000000,3c000000,3c000000
  //   ,3c004020,3d800040,3c008100,bc000000,3ca04020,3d000040,3c080080
  //   ,43c000000,3c002020,3e010002,3c002020,3c004080,3e010002,13c008010
  //   ,3c000000,3c000000,3c004020,3d800040,3c008100,3c400001,3c002020
  //   ,3d000040,3c008011,3c002020,3d000040,13c008800,6*3c000000,3c004020
  //   ,3d800040,3c008100,13c400000,12*3c000000,3c004020,3d800040,3c008100
  //   ,13c200000,12*3c000000,3c004020,3d800040,3c008100,13c000000,12*3c000000
  //   ,3c004020,3d800040,3c008100,13c000000,12*3c000000,3c004020,3d800040
  //   ,3c008100,13c000000,12*3c000000,3c004020,3d800040,3c008100,13c000000
  //   ,12*3c000000,3c004020,3d800040,3c008100,3c002020,3c020080,13e010002
  //   ,10*3c000000,3c004020,3d800040,3c008100,3c000001,3c002020,3d000040
  //   ,13c008200,9*3c000000,3c004020,3d800040,3c008100,13c020008,12*3c000000
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  //   ALU
  //   MPU
  //   contents of ROM (hex, n*v repeats v):
  //   30,3f4,46,45,e43,f15,9,efe20,e0042,249,f15,1,2f220,2012,49,f15
  //   ,2,f020,10012,49,f15,3,f020,115,1ffffa0,10012,149,f15,4,1f120
  //   ,315,ff,31012,2311,1111,31328,32012,11,115,14,1020,11,115,3000001
  //   ,102f,500031,41,30,31,49,f15,3,f020,11,115,13,1020,11,115,0,102f
  //   ,500031,55,30,41,49,f15,1,f020,11,34,11f,49,115,0,10012,49,f15
  //   ,5,f020,115,1,10012,30,11a,49,f15,3,f020,11,115,18,1020,11,115
  //   ,0,102f,200031,72,30,65,49,115,0,10012,49,f15,5,f020,115,1,10012
  //   ,30,11a,15,1ffffdc,111,215,1,12120,215,ffff,12128,10012,11,115
  //   ,0,102f,500031,8b,30,84,15,1ffffdc,115,1,10012,30,8b,15,1ffffdc
  //   ,11,115,1ffffdd,1111,1024,149,f15,1,1f120,1111,102a,115,a5000000
  //   ,102a,149,f15,6,1f120,1012,15,1ffffde,11,115,1,102f,500031,b1
  //   ,30,aa,49,f15,2,f020,11,30,bc,49,f15,3,f020,11,115,12,1020,11
  //   ,30,bc,149,f15,7,1f120,1012,1011,149,f15,6,1f120,1111,34,135,149
  //   ,f15,8,1f120,1012,1011,115,0,102f,500031,e3,30,d6,49,115,0,10012
  //   ,49,f15,5,f020,115,1,10012,30,118,15,1ffffde,11,115,1,102f,500031
  //   ,fd,30,ed,49,f15,8,f020,11,149,1012,49,f15,5,f020,115,1,10012
  //   ,30,118,49,f15,8,f020,11,149,f15,3,1f120,1111,215,12,12120,1012
  //   ,49,115,0,10012,49,f15,5,f020,115,1,10012,30,118,30,11a,49,11
  //   ,44,47,36,115,1ffffba,1211,315,1,23220,315,1f,23228,315,1ffffbb
  //   ,3311,2302f,200031,134,1311,a15,1ffffbc,3a320,3012,21012,36,46
  //   ,45,e43,f15,d,efe20,e0042,249,f15,1,2f220,2012,49,f15,2,f020,10012
  //   ,49,f15,3,f020,115,1ffffa0,10012,111,215,15,12120,1111,249,f15
  //   ,4,2f220,12012,11,115,18,1020,11,115,0,102f,500031,1af,30,163
  //   ,49,f15,3,f020,11,115,14,1020,11,115,3000001,102f,500031,1af,30
  //   ,173,49,f15,4,f020,11,34,80b,115,0,102f,200031,1af,30,181,49,f15
  //   ,3,f020,11,115,16,1020,11,115,0,102f,200031,1a3,30,191,49,f15
  //   ,3,f020,11,115,16,1020,11,34,80b,115,0,102f,200031,1af,30,1a3
  //   ,49,f15,1,f020,11,115,11,102f,300031,1bc,30,1af,49,115,0,10012
  //   ,49,f15,5,f020,115,1,10012,30,2f7,49,f15,1,f020,11,115,12,1021
  //   ,149,f15,6,1f120,1012,1011,11,249,f15,3,2f220,2311,a15,11,3a320
  //   ,3012,1011,115,1,1020,11,2111,215,10,12120,1012,49,f15,7,f020
  //   ,115,0,10012,30,1e7,49,f15,7,f020,11,115,10,102f,100031,1fc,30
  //   ,1f3,49,f15,5,f020,115,2,10012,30,220,49,f15,6,f020,11,149,f15
  //   ,7,1f120,1211,2020,215,2,2020,11,249,f15,3,2f220,2211,1111,21120
  //   ,1012,30,215,49,f15,7,f020,111,215,1,12120,10012,30,1e7,49,f15
  //   ,3,f020,11,115,19,1020,11,115,0,102f,500031,240,30,230,49,f15
  //   ,8,f020,115,1,10012,49,f15,9,f020,115,2030000,10012,30,250,49
  //   ,f15,8,f020,115,0,10012,49,f15,9,f020,115,2020000,10012,30,250
  //   ,49,f15,a,f020,115,0,10012,30,259,49,f15,a,f020,11,115,12,102f
  //   ,100031,26e,30,265,49,f15,5,f020,115,5,10012,30,295,49,f15,6,f020
  //   ,11,149,f15,a,1f120,1211,2020,11,249,f15,b,2f220,2012,2011,249
  //   ,f15,9,2f220,2211,1111,21120,1012,30,28a,49,f15,a,f020,111,215
  //   ,1,12120,10012,30,259,49,f15,4,f020,11,149,f15,9,1f120,1211,315
  //   ,1,23220,2012,49,f15,2,f020,11,1111,215,2,12120,1012,49,f15,1
  //   ,f020,11,149,f15,3,1f120,1211,a15,17,2a220,2012,1011,215,18,2020
  //   ,30012,49,f15,8,f020,11,1211,315,19,23220,2012,1011,115,16,1020
  //   ,11,149,f15,c,1f120,1012,1011,115,0,102f,200031,2e4,30,2dc,49
  //   ,f15,c,f020,11,60,30,2e4,49,f15,9,f020,11,115,12,1020,149,1012
  //   ,49,f15,5,f020,115,1,10012,30,2f7,49,11,44,47,36,46,45,e43,f15
  //   ,4,efe20,e0042,49,115,1ffffa0,10012,149,f15,1,1f120,215,2010000
  //   ,21012,211,315,11,23220,2211,1311,23012,11,215,10,2020,11,1111
  //   ,215,1,12120,1012,49,f15,2,f020,115,0,10012,30,328,49,f15,2,f020
  //   ,11,115,10,102f,100031,336,30,334,30,357,49,11,149,f15,2,1f120
  //   ,1211,2020,11,249,f15,1,2f220,2211,1111,21120,215,2,12120,1012
  //   ,30,34c,49,f15,2,f020,111,215,1,12120,10012,30,328,49,f15,1,f020
  //   ,11,115,12,1020,249,f15,3,2f220,2012,49,311,a15,18,3a320,a15,0
  //   ,a3012,311,b15,17,3b320,a3012,2311,11,1020,30012,2011,44,47,36
  //   ,46,45,e43,f15,5,efe20,e0042,149,f15,1,1f120,1012,49,f15,2,f020
  //   ,115,1ffff86,10012,49,f15,3,f020,115,1ffffa0,10012,15,1ffffde
  //   ,11,115,0,102f,500031,3c5,30,39d,49,f15,1,f020,11,149,f15,2,1f120
  //   ,1211,315,12,23220,2012,1011,115,13,1020,115,1,10012,15,1ffffde
  //   ,10012,49,f15,3,f020,11,3020,11,249,2012,49,f15,4,f020,10012,30
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  //   contents of UROM (hex, n*v repeats v):
  //   30,8000008,15,7,3b,37,842,f0,e15,a000000,e0042,e0048,e43,f15,25
  //   ,efe20,e0042,e49,f15,5,efe20,4e012,e49,f15,4,efe20,5e012,e49,f15
  //   ,3,efe20,6e012,e49,f15,2,efe20,7e012,e49,f15,1,efe20,8e012,e49
  //   ,9e012,15,9ffffd8,115,45,10012,10510,15,9ffffd9,215,6e,20012,115
  //   ,9ffffda,715,74,71012,115,9ffffdb,315,65,31012,115,9ffffdc,b15
  //   ,72,b1012,a15,9ffffdd,615,20,6a012,a15,9ffffde,3a012,a15,9ffffdf
  //   ,15,78,e49,f15,c,efe20,e012,a012,a15,9ffffe0,15,70,a012,d10,a15
  //   ,9ffffe1,ba012,a15,9ffffe2,3a012,a15,9ffffe3,15,73,e49,f15,7,efe20
  //   ,e012,a012,a15,9ffffe4,a012,a15,9ffffe5,15,69,a012,910,a15,9ffffe6
  //   ,15,6f,e49,f15,19,efe20,e012,a012,a15,9ffffe7,2a012,a15,9ffffe8
  //   ,c15,2c,ca012,a15,9ffffe9,6a012,a15,9ffffea,3a012,a15,9ffffeb
  //   ,2a012,a15,9ffffec,815,64,8a012,e49,f15,e,efe20,8e012,a15,9ffffed
  //   ,6a012,a15,9ffffee,15,77,e49,f15,13,efe20,e012,a012,a15,9ffffef
  //   ,9a012,a15,9fffff0,7a012,a15,9fffff1,15,68,e49,f15,b,efe20,e012
  //   ,a012,a15,9fffff2,6a012,a15,9fffff3,c15,3c,ca012,a15,9fffff4,50010
  //   ,e49,f15,f,efe20,e012,a012,a15,9fffff5,2a012,a15,9fffff6,7a012
  //   ,a15,9fffff7,3a012,a15,9fffff8,ba012,a15,9fffff9,c15,3e,ca012
  //   ,a15,9fffffa,415,3a,4a012,a15,9fffffb,115,a,e49,f15,6,efe20,1e012
  //   ,1a012,a15,9fffffc,ca012,a15,9fffffd,ca012,a15,9fffffe,6a012,a15
  //   ,9ffffff,515,0,5a012,a15,9ffffb8,115,49,e49,f15,1a,efe20,1e012
  //   ,1a012,a15,9ffffb9,2a012,a15,9ffffba,e49,f15,10,efe20,de012,da012
  //   ,a15,9ffffbb,115,75,1a012,a15,9ffffbc,7a012,a15,9ffffbd,a012,a15
  //   ,9ffffbe,ba012,a15,9ffffbf,ba012,a15,9ffffc0,e49,f15,19,ef017
  //   ,a012,a15,9ffffc1,ba012,a15,9ffffc2,4a012,a15,9ffffc3,6a012,a15
  //   ,9ffffc4,c15,4e,ca012,a15,9ffffc5,a012,a15,9ffffc6,6a012,a15,9ffffc7
  //   ,9a012,a15,9ffffc8,2a012,a15,9ffffc9,da012,a15,9ffffca,e49,f15
  //   ,1b,efe20,1e012,1a012,a15,9ffffcb,e49,f15,12,efe20,7e012,7a012
  //   ,a15,9ffffcc,6a012,a15,9ffffcd,ba012,a15,9ffffce,3a012,a15,9ffffcf
  //   ,15,63,e49,f15,15,efe20,e012,a012,a15,9ffffd0,3a012,a15,9ffffd1
  //   ,9a012,a15,9ffffd2,15,76,e49,f15,14,efe20,e012,a012,a15,9ffffd3
  //   ,3a012,a15,9ffffd4,8a012,a15,9ffffd5,15,2e,a012,a15,9ffffd6,e49
  //   ,f15,6,efd17,da012,a15,9ffffd7,5a012,a15,9ffffb2,c15,51,ca012
  //   ,a15,9ffffb3,1a012,a15,9ffffb4,9a012,a15,9ffffb5,7a012,a15,9ffffb6
  //   ,a012,110,e49,f15,18,efe20,1e012,a15,9ffffb7,5a012,a15,9ffff8a
  //   ,da012,a15,9ffff8b,c15,57,ca012,c15,9ffff8c,15,61,e49,f15,a,efe20
  //   ,e012,c012,c15,9ffff8d,bc012,c15,9ffff8e,20810,8c012,c15,9ffff8f
  //   ,9c012,90a10,e49,f15,16,efe20,ae012,c15,9ffff90,8c012,c15,9ffff91
  //   ,15,67,e49,f15,1e,efe20,e012,c012,c15,9ffff92,4c012,40910,c15
  //   ,9ffff93,6c012,c15,9ffff94,d15,54,dc012,c15,9ffff95,e49,f15,b
  //   ,ef017,c012,c15,9ffff96,3c012,c15,9ffff97,bc012,c15,9ffff98,3c012
  //   ,c15,9ffff99,215,27,e49,f15,17,efe20,2e012,2c012,c15,9ffff9a,bc012
  //   ,c15,9ffff9b,3c012,c15,9ffff9c,6c012,c15,9ffff9d,8c012,c15,9ffff9e
  //   ,e49,f15,19,ef717,7c012,c15,9ffff9f,6c012,c15,9ffffa0,c012,c15
  //   ,9ffffa1,ac012,c15,9ffffa2,e49,f15,7,ef417,4c012,c15,9ffffa3,e49
  //   ,f15,12,ef217,2c012,c15,9ffffa4,7c012,c15,9ffffa5,bc012,c15,9ffffa6
  //   ,15,79,c012,a10,e49,f15,11,efe20,ae012,c15,9ffffa7,6c012,c15,9ffffa8
  //   ,e49,f15,a,efd17,dc012,c15,9ffffa9,8c012,c15,9ffffaa,4c012,c15
  //   ,9ffffab,e49,f15,13,ef017,c012,c15,9ffffac,3c012,c15,9ffffad,bc012
  //   ,c15,9ffffae,4c012,c15,9ffffaf,1c012,c15,9ffffb0,e49,f15,6,ef117
  //   ,1c012,c15,9ffffb1,e49,f15,8,efe20,5e012,5c012,c15,9ffff88,1c012
  //   ,10410,c15,9ffff89,5c012,c15,9ffff6a,15,53,c012,e49,f15,d,efe20
  //   ,e012,c15,9ffff6b,ac012,c15,9ffff6c,8c012,c15,9ffff6d,2c012,20510
  //   ,c15,9ffff6e,dc012,c15,9ffff6f,e49,f15,c,ef217,2c012,c15,9ffff70
  //   ,e49,f15,f,efd17,dc012,c15,9ffff71,bc012,c15,9ffff72,bc012,c15
  //   ,9ffff73,7c012,c15,9ffff74,bc012,c15,9ffff75,90a10,e49,f15,21
  //   ,efe20,ae012,ac012,c15,9ffff76,60910,9c012,c15,9ffff77,15,55,e49
  //   ,f15,1c,efe20,e012,c012,c15,9ffff78,8c012,c15,9ffff79,e49,f15
  //   ,9,efe20,3e012,3c012,c15,9ffff7a,2c012,c15,9ffff7b,e49,f15,10
  //   ,ef617,6c012,c15,9ffff7c,3c012,c15,9ffff7d,e49,f15,15,ef117,1c012
  //   ,c15,9ffff7e,50110,1c012,c15,9ffff7f,3c012,c15,9ffff80,e49,f15
  //   ,e,ef517,5c012,c15,9ffff81,9c012,c15,9ffff82,e49,f15,17,ef317
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endmodule
