// Digital circuit aurora-32.dig as structural Verilog
module aurora_32 (
  input  Clock,
  input  clock_1000hz,
  output [31:0] KSP,
  output [3:0] STATE,
  output [7:0] IR,
  output [31:0] PC,
  output [31:0] KFP,
  output [31:0] USP,
  output [31:0] UFP
);

  wire add_1_c_o, and_1_out, and_2_out, and_5_out, and_6_out, and_7_out, and_8_out, and_9_out, and_10_out,
       and_11_out, and_12_out, and_13_out, and_14_out, and_15_out, and_16_out, and_17_out, and_18_out,
       and_19_out, and_20_out, and_21_out, and_22_out, and_23_out, and_24_out, and_25_out, and_26_out,
       and_27_out, and_28_out, and_29_out, and_30_out, and_31_out, and_32_out, and_33_out, and_34_out,
       and_35_out, and_36_out, and_37_out, and_38_out, and_39_out, AV_IInstERR, AV_Keyboard, AV_MEMERR,
       AV_Telnet, AV_Tick, bitselector_1_out, clock_t, CLR_IE, CLR_KernelMode, comparator_1_eq,
       comparator_2_eq, comparator_3_eq, comparator_4_eq, comparator_5_eq, comparator_6_eq, comparator_6_lt,
       comparator_7_eq, comparator_7_lt, comparator_8_eq, comparator_9_eq, CS_Gr, CS_Grbgcolor, CS_Grcolor,
       CS_Grdatahigh, CS_Grdatalow, CS_Grh, CS_Grmode, CS_Grstat, CS_Grw, CS_Grx, CS_Gry, CS_IVT,
       CS_KeyBoard, CS_MIDI, CS_RAM, CS_ROM, CS_Stack, CS_Telnet, CS_Terminal, CS_Tick, CS_Timer, CS_URAM,
       CS_UROM, CS_UStack, decoder_1_out_0, decoder_1_out_1, delay_1_out, delay_2_out, delay_3_out,
       delay_4_out, delay_5_out, delay_6_out, DN_SP, driverinvsel_1_out, EN_KSP, EN_USP, END_CYCLE, Flag_c,
       Flag_n, Flag_v, Flag_v_Bus, Flag_z, HALT, INC_PC, INT_REQ, INT_RET, INT_TAKE, Kernel_Mode,
       Kernel_Use_USP, KernelMode_Bus, LD_FP, LD_IR, LD_KFP, LD_KSP, LD_MAR, LD_MDREXT, LD_MDRINT, LD_PC,
       LD_RFlags, LD_Rflags_Bus, LD_Rw, LD_SP, LD_UFP, LD_USP, multiplexer_4_out, multiplexer_9_out,
       multiplexer_11_out, multiplexer_12_out, multiplexer_13_out, multiplexer_14_out, multiplexer_15_out,
       multiplexer_16_out, multiplexer_18_out, nor_2_out, not_1_out, not_2_out, not_3_out, not_4_out,
       not_6_out, not_7_out, not_8_out, not_9_out, not_10_out, not_11_out, not_12_out, not_13_out,
       not_14_out, not_15_out, not_17_out, not_18_out, not_19_out, not_20_out, not_21_out, not_22_out,
       not_23_out, not_24_out, nPSR_q, OE, OE_ALU, OE_FP, OE_INT_REQ, OE_KFP, OE_KSP, OE_MDREXT, OE_MDRINT,
       OE_PC, OE_Ra, OE_Rb, OE_Rflags, OE_SP, OE_UFP, OE_USP, or_1_out, or_6_out, or_7_out, or_8_out,
       or_9_out, or_10_out, or_11_out, or_12_out, or_13_out, or_14_out, or_15_out, R_IE_q, SET_IE,
       SET_KernelMode, Sign_A, Sign_B, Sign_R, SignedCalc, sub_1_c_o, Tick_ovf, UP_SP, Use_USP, WE,
       xnor_2_out, xor_2_out, xor_3_out, xor_4_out, xor_5_out, xor_6_out;
  wire [0:0] d_ff_as_1_q;
  wire [2:0] priorityencoder_1_num;
  wire [3:0] ADDR_Ra, ADDR_Rb, ADDR_Rw, MODE_ALU;
  wire [5:0] add_4_s;
  wire [6:0] RegFile_db;
  wire [7:0] telnet_1_out;
  wire [15:0] keyboard_1_d;
  wire [30:0] multiplexer_10_out, RegFile_da;
  wire [30:7] RegFile_db_2;
  wire [31:0] add_1_s, add_2_s, add_3_s, add_5_s, and_4_out, Dec_s, Div_S_q, Div_S_r, Div_U_q, Div_U_r,
       driver_1_out, driver_12_out, Gr_Conx_out, Gr_Cony_out, Gr_d, Inc_s, INT_ADDR, MAR_q, MDR_EXT_q,
       MDR_INT_q, multiplexer_5_out, multiplexer_7_out, multiplexer_8_out, multiplexer_17_out, nand_1_out,
       nor_1_out, not_5_out, or_5_out, register_1_q, register_2_q, register_3_q, register_4_q, register_5_q,
       register_6_q, register_7_q, register_8_q, register_9_q, Shift_S_out, Shift_U_out, sub_1_s, Timer_out,
       xnor_1_out, xor_1_out;
  wire [31:6] add_4_s_2;
  wire [31:20] IR_q;
  wire [32:23] multiplexer_3_out;
  wire [34:0] CU_K_d, multiplexer_1_out, multiplexer_2_out;
  wire [35:0] CU_U_d;
  wire [36:0] CU_INT_d;
  wire [63:0] mul_1_mul, mul_2_mul, Mul_S_mul, Mul_U_mul, multiplexer_6_out;

  assign {driver_1_out[31:5], KernelMode_Bus, Flag_v_Bus, driver_1_out[2:0]} = OE_Rflags ? {{27{1'b0}}, Kernel_Mode, Flag_v, Flag_n, Flag_c, Flag_z} : 32'bz;  // Driver driver_1
  assign {driver_1_out[31:5], KernelMode_Bus, Flag_v_Bus, driver_1_out[2:0]} = OE_INT_REQ ? INT_ADDR : 32'bz;  // Driver driver_2
  CounterPreset #(.maxValue(15), .Bits(4)) u_STATE (
    .en(1'b1), .C(clock_t), .dir(1'b0), .in(4'b0000), .ld(1'b0), .clr(END_CYCLE), .out(STATE));  // open: ovf
  Register #(.Bits(32)) u_IR (
    .D({driver_1_out[31:5], KernelMode_Bus, Flag_v_Bus, driver_1_out[2:0]}), .C(clock_t), .en(LD_IR),
    .Q({IR_q, ADDR_Ra, ADDR_Rb, ADDR_Rw, IR}));
  assign {driver_1_out[31:5], KernelMode_Bus, Flag_v_Bus, driver_1_out[2:0]} = OE_PC ? PC : 32'bz;  // Driver driver_3
  assign {driver_1_out[31:5], KernelMode_Bus, Flag_v_Bus, driver_1_out[2:0]} = OE_Ra ? {Sign_A, RegFile_da} : 32'bz;  // Driver driver_4
  RegisterFile #(.AddrBits(4), .Bits(32)) RegFile (
    .Din({driver_1_out[31:5], KernelMode_Bus, Flag_v_Bus, driver_1_out[2:0]}), .we(LD_Rw), .Rw(ADDR_Rw),
    .C(clock_t), .Ra(ADDR_Ra), .Rb(ADDR_Rb), .Da({Sign_A, RegFile_da}),
    .Db({Sign_B, RegFile_db_2, RegFile_db}));
  assign {driver_1_out[31:5], KernelMode_Bus, Flag_v_Bus, driver_1_out[2:0]} = OE_Rb ? {Sign_B, RegFile_db_2, RegFile_db} : 32'bz;  // Driver driver_5
  CounterPreset #(.Bits(32)) u_KSP (
    .en(EN_KSP), .C(clock_t), .dir(DN_SP),
    .in({driver_1_out[31:5], KernelMode_Bus, Flag_v_Bus, driver_1_out[2:0]}), .ld(LD_KSP), .clr(1'b0),
    .out(KSP));  // open: ovf
  assign {driver_1_out[31:5], KernelMode_Bus, Flag_v_Bus, driver_1_out[2:0]} = OE_KSP ? KSP : 32'bz;  // Driver driver_6
  CounterPreset #(.Bits(32)) u_USP (
    .en(EN_USP), .C(clock_t), .dir(DN_SP),
    .in({driver_1_out[31:5], KernelMode_Bus, Flag_v_Bus, driver_1_out[2:0]}), .ld(LD_USP), .clr(1'b0),
    .out(USP));  // open: ovf
  assign {driver_1_out[31:5], KernelMode_Bus, Flag_v_Bus, driver_1_out[2:0]} = OE_USP ? USP : 32'bz;  // Driver driver_7
  Register #(.Bits(32)) u_KFP (
    .D({driver_1_out[31:5], KernelMode_Bus, Flag_v_Bus, driver_1_out[2:0]}), .C(clock_t), .en(LD_KFP), .Q(KFP));
  assign {driver_1_out[31:5], KernelMode_Bus, Flag_v_Bus, driver_1_out[2:0]} = OE_KFP ? KFP : 32'bz;  // Driver driver_8
  Register #(.Bits(32)) u_UFP (
    .D({driver_1_out[31:5], KernelMode_Bus, Flag_v_Bus, driver_1_out[2:0]}), .C(clock_t), .en(LD_UFP), .Q(UFP));
  assign {driver_1_out[31:5], KernelMode_Bus, Flag_v_Bus, driver_1_out[2:0]} = OE_UFP ? UFP : 32'bz;  // Driver driver_9
  CounterPreset #(.Bits(32), .isProgramCounter("true")) u_PC (
    .en(INC_PC), .C(clock_t), .dir(1'b0),
    .in({driver_1_out[31:5], KernelMode_Bus, Flag_v_Bus, driver_1_out[2:0]}), .ld(LD_PC), .clr(1'b0), .out(PC));  // open: ovf
  JK_FF_AS jk_ff_as_1 (
    .Set(and_1_out), .J(1'b0), .C(clock_t), .K(OE_INT_REQ), .Clr(1'b0), .Q(AV_IInstERR));  // open: nQ
  ROM #(.AddrBits(4), .Bits(37)) CU_INT (.A(STATE), .sel(1'b1), .D(CU_INT_d));
  ROM #(.AddrBits(12), .isProgramMemory("true"), .Bits(36)) CU_U (.A({IR, STATE}), .sel(1'b1), .D(CU_U_d));
  ROM #(.AddrBits(12), .isProgramMemory("true"), .Bits(37)) CU_K (
    .A({IR, STATE}), .sel(1'b1), .D({HALT, Kernel_Use_USP, CU_K_d}));
  or or_1 (or_1_out, UP_SP, DN_SP);
  Comparator #(.Bits(8)) comparator_1 (.a(IR), .b(8'h33), .eq(comparator_1_eq));  // open: gt, lt
  Multiplexer #(.Bits(37)) multiplexer_1 (
    .sel(INT_TAKE), .in_0({37{1'b0}}), .in_1(CU_INT_d), .out({INT_RET, OE_INT_REQ, multiplexer_1_out}));
  not not_1 (not_1_out, Kernel_Mode);
  assign {driver_1_out[31:5], KernelMode_Bus, Flag_v_Bus, driver_1_out[2:0]} = OE_ALU ? {Sign_R, multiplexer_10_out} : 32'bz;  // Driver driver_10
  Demultiplexer demultiplexer_1 (.sel(Use_USP), .in(OE_SP), .out_0(OE_KSP), .out_1(OE_USP));
  Demultiplexer demultiplexer_2 (.sel(Use_USP), .in(LD_SP), .out_0(LD_KSP), .out_1(LD_USP));
  Demultiplexer demultiplexer_3 (.sel(Use_USP), .in(or_1_out), .out_0(EN_KSP), .out_1(EN_USP));
  Demultiplexer demultiplexer_4 (.sel(Use_USP), .in(OE_FP), .out_0(OE_KFP), .out_1(OE_UFP));
  Demultiplexer demultiplexer_5 (.sel(Use_USP), .in(LD_FP), .out_0(LD_KFP), .out_1(LD_UFP));
  and and_1 (and_1_out, not_1_out, CU_U_d[35]);
  Multiplexer #(.Bits(35)) multiplexer_2 (
    .sel(Kernel_Mode), .in_0(CU_U_d[34:0]), .in_1(CU_K_d), .out(multiplexer_2_out));
  assign driverinvsel_1_out = ~comparator_1_eq ? and_6_out : 1'bz;  // DriverInvSel driverinvsel_1
  or or_2 (INC_PC, multiplexer_3_out[23], driverinvsel_1_out);
  Multiplexer #(.Bits(35)) multiplexer_3 (
    .sel(INT_TAKE), .in_0(multiplexer_2_out), .in_1(multiplexer_1_out),
    .out({SET_KernelMode, CLR_KernelMode, multiplexer_3_out[32:31], SignedCalc, MODE_ALU, WE, OE, multiplexer_3_out[23], SET_IE, CLR_IE, OE_ALU, OE_Rflags, OE_Rb, OE_Ra, OE_MDREXT, OE_MDRINT, OE_PC, OE_SP, OE_FP, LD_Rflags_Bus, LD_RFlags, LD_Rw, LD_IR, LD_MDREXT, LD_MDRINT, LD_MAR, LD_PC, LD_SP, LD_FP, UP_SP, DN_SP}));
  not not_2 (not_2_out, HALT);
  or or_3 (Use_USP, Kernel_Use_USP, not_3_out);
  not not_3 (not_3_out, Kernel_Mode);
  or or_4 (END_CYCLE, and_6_out, multiplexer_3_out[32]);
  not not_4 (not_4_out, Flag_z);
  and and_2 (and_2_out, not_4_out, not_13_out);
  and and_3 (clock_t, Clock, not_2_out);
  Add #(.Bits(32)) add_1 (
    .a({Sign_A, RegFile_da}), .b({Sign_B, RegFile_db_2, RegFile_db}), .c_i(1'b0), .s(add_1_s), .c_o(add_1_c_o));
  Sub #(.Bits(32)) sub_1 (
    .a({Sign_A, RegFile_da}), .b({Sign_B, RegFile_db_2, RegFile_db}), .c_i(1'b0), .s(sub_1_s), .c_o(sub_1_c_o));
  BarrelShifter #(.Bits(32), .barrelSigned("true")) Shift_U (
    .in({Sign_A, RegFile_da}), .shift(RegFile_db), .out(Shift_U_out));
  assign and_4_out = {Sign_A, RegFile_da} & {Sign_B, RegFile_db_2, RegFile_db};  // And and_4, 32 bits wide
  assign nand_1_out = ~({Sign_A, RegFile_da} & {Sign_B, RegFile_db_2, RegFile_db});  // NAnd nand_1, 32 bits wide
  assign or_5_out = {Sign_A, RegFile_da} | {Sign_B, RegFile_db_2, RegFile_db};  // Or or_5, 32 bits wide
  assign nor_1_out = ~({Sign_A, RegFile_da} | {Sign_B, RegFile_db_2, RegFile_db});  // NOr nor_1, 32 bits wide
  assign xor_1_out = {Sign_A, RegFile_da} ^ {Sign_B, RegFile_db_2, RegFile_db};  // XOr xor_1, 32 bits wide
  assign xnor_1_out = ~({Sign_A, RegFile_da} ^ {Sign_B, RegFile_db_2, RegFile_db});  // XNOr xnor_1, 32 bits wide
  assign not_5_out = ~{Sign_A, RegFile_da};  // Not not_5, 32 bits wide
  Add #(.Bits(32)) Inc (.a({Sign_A, RegFile_da}), .b(32'h1), .c_i(1'b0), .s(Inc_s));  // open: c_o
  Sub #(.Bits(32)) Dec (.a({Sign_A, RegFile_da}), .b(32'h1), .c_i(1'b0), .s(Dec_s));  // open: c_o
  not not_6 (not_6_out, Flag_c);
  and and_5 (and_5_out, not_6_out, not_7_out);
  not not_7 (not_7_out, Flag_z);
  not not_8 (not_8_out, Flag_c);
  not not_9 (not_9_out, Flag_z);
  not not_10 (not_10_out, and_5_out);
  xor xor_2 (xor_2_out, Flag_n, Flag_v);
  not not_11 (not_11_out, xor_2_out);
  not not_12 (not_12_out, and_2_out);
  not not_13 (not_13_out, xor_2_out);
  BarrelShifter #(.Bits(32), .barrelShifterMode("arithmetic"), .barrelSigned("true")) Shift_S (
    .in({Sign_A, RegFile_da}), .shift(RegFile_db), .out(Shift_S_out));
  Multiplexer #(.Selector_Bits(4)) multiplexer_4 (
    .sel(IR_q[23:20]), .in_0(1'b0), .in_1(Flag_c), .in_2(Flag_z), .in_3(and_5_out), .in_4(not_8_out),
    .in_5(not_9_out), .in_6(not_10_out), .in_7(Flag_n), .in_8(Flag_v), .in_9(xor_2_out), .in_10(not_11_out),
    .in_11(and_2_out), .in_12(not_12_out), .in_13(1'b0), .in_14(1'b0), .in_15(1'b0), .out(multiplexer_4_out));
  not not_14 (not_14_out, multiplexer_4_out);
  Mul #(.Bits(32)) Mul_U (.a({Sign_A, RegFile_da}), .b({Sign_B, RegFile_db_2, RegFile_db}), .mul(Mul_U_mul));
  Mul #(.Signed("true"), .Bits(32)) Mul_S (
    .a({Sign_A, RegFile_da}), .b({Sign_B, RegFile_db_2, RegFile_db}), .mul(Mul_S_mul));
  Div #(.Bits(32)) Div_U (.a({Sign_A, RegFile_da}), .b({Sign_B, RegFile_db_2, RegFile_db}), .q(Div_U_q), .r(Div_U_r));
  Div #(.remainderPositive("false"), .Signed("true"), .Bits(32)) Div_S (
    .a({Sign_A, RegFile_da}), .b({Sign_B, RegFile_db_2, RegFile_db}), .q(Div_S_q), .r(Div_S_r));
  Multiplexer #(.Bits(32)) multiplexer_5 (
    .sel(SignedCalc), .in_0(Shift_U_out), .in_1(Shift_S_out), .out(multiplexer_5_out));
  and and_6 (and_6_out, multiplexer_3_out[31], not_14_out);
  Multiplexer #(.Bits(64)) multiplexer_6 (
    .sel(SignedCalc), .in_0(Mul_U_mul), .in_1(Mul_S_mul), .out(multiplexer_6_out));
  RS_FF R_IE (.S(SET_IE), .C(clock_t), .R(CLR_IE), .Q(R_IE_q));  // open: nQ
  xor xor_3 (xor_3_out, SET_KernelMode, CLR_KernelMode);
  Multiplexer #(.Bits(32)) multiplexer_7 (.sel(SignedCalc), .in_0(Div_U_q), .in_1(Div_S_q), .out(multiplexer_7_out));
  Multiplexer #(.Bits(32)) multiplexer_8 (.sel(SignedCalc), .in_0(Div_U_r), .in_1(Div_S_r), .out(multiplexer_8_out));
  Multiplexer multiplexer_9 (.sel(LD_Rflags_Bus), .in_0(CLR_KernelMode), .in_1(not_15_out), .out(multiplexer_9_out));
  not not_15 (not_15_out, KernelMode_Bus);
  or or_6 (or_6_out, xor_3_out, LD_Rflags_Bus);
  and and_7 (and_7_out, END_CYCLE, INT_REQ, R_IE_q);
  Register nPSR (.D(multiplexer_9_out), .C(clock_t), .en(or_6_out), .Q(nPSR_q));
  Register #(.Bits(32)) MAR (
    .D({driver_1_out[31:5], KernelMode_Bus, Flag_v_Bus, driver_1_out[2:0]}), .C(clock_t), .en(LD_MAR),
    .Q(MAR_q));
  assign {driver_1_out[31:5], KernelMode_Bus, Flag_v_Bus, driver_1_out[2:0]} = OE_MDRINT ? MDR_INT_q : 32'bz;  // Driver driver_11
  not not_16 (Kernel_Mode, nPSR_q);
  Decoder decoder_1 (.sel(MAR_q[31]), .out_0(decoder_1_out_0), .out_1(decoder_1_out_1));
  Register #(.Bits(32)) MDR_EXT (
    .D({driver_1_out[31:5], KernelMode_Bus, Flag_v_Bus, driver_1_out[2:0]}), .C(clock_t), .en(LD_MDREXT),
    .Q(MDR_EXT_q));
  RS_FF rs_ff_1 (.S(and_7_out), .C(clock_t), .R(INT_RET), .Q(INT_TAKE));  // open: nQ
  Multiplexer #(.Selector_Bits(4), .Bits(32)) multiplexer_10 (
    .sel(MODE_ALU), .in_0(add_1_s), .in_1(sub_1_s), .in_2(multiplexer_6_out[31:0]), .in_3(multiplexer_7_out),
    .in_4(multiplexer_5_out), .in_5(and_4_out), .in_6(nand_1_out), .in_7(or_5_out), .in_8(nor_1_out),
    .in_9(xor_1_out), .in_10(xnor_1_out), .in_11(not_5_out), .in_12(Inc_s), .in_13(Dec_s),
    .in_14(multiplexer_8_out), .in_15({32{1'b0}}), .out({Sign_R, multiplexer_10_out}));
  xnor xnor_2 (xnor_2_out, Sign_A, Sign_B);
  xor xor_4 (xor_4_out, Sign_A, Sign_B);
  Delay delay_1 (.in(driver_1_out[31]), .out(delay_1_out));
  not not_17 (not_17_out, Kernel_Mode);
  and and_8 (and_8_out, decoder_1_out_0, Kernel_Mode);
  Register #(.Bits(32)) MDR_INT (.D(driver_12_out), .C(clock_t), .en(LD_MDRINT), .Q(MDR_INT_q));
  assign driver_12_out = OE_MDREXT ? MDR_EXT_q : 32'bz;  // Driver driver_12
  xor xor_5 (xor_5_out, Sign_A, Sign_R);
  xor xor_6 (xor_6_out, Sign_A, Sign_R);
  and and_9 (and_9_out, delay_1_out, not_17_out);
  Demultiplexer #(.Selector_Bits(4)) demultiplexer_6 (
    .sel(MAR_q[27:24]), .in(and_8_out), .out_0(CS_ROM), .out_1(CS_RAM), .out_2(CS_Stack), .out_3(CS_IVT),
    .out_4(CS_KeyBoard), .out_5(CS_Terminal), .out_6(CS_Telnet), .out_7(CS_Tick), .out_8(CS_Timer),
    .out_9(CS_Gr), .out_10(CS_MIDI));  // open: out_11, out_12, out_13, out_14, out_15
  Comparator #(.Bits(4)) comparator_2 (.a(MODE_ALU), .b(4'b0001), .eq(comparator_2_eq));  // open: gt, lt
  and and_10 (and_10_out, xnor_2_out, xor_5_out);
  and and_11 (and_11_out, xor_4_out, xor_6_out);
  and and_12 (and_12_out, WE, CS_Grx);
  and and_13 (and_13_out, WE, CS_Gry);
  and and_14 (and_14_out, WE, CS_Grcolor);
  and and_15 (and_15_out, WE, CS_Grw);
  and and_16 (and_16_out, WE, CS_Grh);
  assign driver_12_out = and_18_out ? {{31{1'b0}}, d_ff_as_1_q[0]} : 32'bz;  // Driver driver_13
  and and_17 (and_17_out, clock_t, WE, CS_Grstat);
  and and_18 (and_18_out, OE, CS_Grstat);
  and and_19 (and_19_out, WE, CS_Grdatalow);
  and and_20 (and_20_out, WE, CS_Grdatahigh);
  and and_21 (and_21_out, WE, CS_Grbgcolor);
  and and_22 (and_22_out, WE, CS_Grmode);
  Comparator #(.Bits(32)) comparator_3 (
    .a({32{1'b0}}), .b({Sign_R, multiplexer_10_out}), .eq(comparator_3_eq));  // open: gt, lt
  Multiplexer multiplexer_11 (
    .sel(not_21_out), .in_0(driver_1_out[1]), .in_1(multiplexer_12_out), .out(multiplexer_11_out));
  Multiplexer multiplexer_12 (.sel(comparator_2_eq), .in_0(add_1_c_o), .in_1(sub_1_c_o), .out(multiplexer_12_out));
  Multiplexer multiplexer_13 (.sel(comparator_2_eq), .in_0(and_10_out), .in_1(and_11_out), .out(multiplexer_13_out));
  and and_23 (and_23_out, LD_MAR, nor_2_out, and_9_out);
  Comparator #(.Bits(7)) comparator_4 (.a(MAR_q[30:24]), .b({7{1'b0}}), .eq(comparator_4_eq));  // open: gt, lt
  not not_18 (not_18_out, comparator_4_eq);
  Comparator #(.Bits(7)) comparator_5 (.a(MAR_q[30:24]), .b(7'b0000011), .eq(comparator_5_eq));  // open: gt, lt
  not not_19 (not_19_out, comparator_5_eq);
  Register #(.Bits(32)) register_1 (.D(driver_12_out), .C(clock_t), .en(and_12_out), .Q(register_1_q));
  Register #(.Bits(32)) register_2 (.D(driver_12_out), .C(clock_t), .en(and_13_out), .Q(register_2_q));
  Register #(.Bits(32)) register_3 (.D(driver_12_out), .C(clock_t), .en(and_14_out), .Q(register_3_q));
  Register #(.Bits(32)) register_4 (.D(driver_12_out), .C(clock_t), .en(and_15_out), .Q(register_4_q));
  Register #(.Bits(32)) register_5 (.D(driver_12_out), .C(clock_t), .en(and_16_out), .Q(register_5_q));
  D_FF_AS d_ff_as_1 (
    .Set(1'b0), .D(driver_12_out[0]), .C(and_17_out), .Clr(comparator_7_eq), .Q(d_ff_as_1_q[0]));  // open: nQ
  Register #(.Bits(32)) register_6 (.D(driver_12_out), .C(clock_t), .en(and_19_out), .Q(register_6_q));
  Register #(.Bits(32)) register_7 (.D(driver_12_out), .C(clock_t), .en(and_20_out), .Q(register_7_q));
  Register #(.Bits(32)) register_8 (.D(driver_12_out), .C(clock_t), .en(and_21_out), .Q(register_8_q));
  Register #(.Bits(32)) register_9 (.D(driver_12_out), .C(clock_t), .en(and_22_out), .Q(register_9_q));
  not not_20 (not_20_out, LD_Rflags_Bus);
  Multiplexer multiplexer_14 (
    .sel(not_20_out), .in_0(driver_1_out[0]), .in_1(comparator_3_eq), .out(multiplexer_14_out));
  not not_21 (not_21_out, LD_Rflags_Bus);
  Multiplexer multiplexer_15 (.sel(not_22_out), .in_0(driver_1_out[2]), .in_1(Sign_R), .out(multiplexer_15_out));
  not not_22 (not_22_out, LD_Rflags_Bus);
  Multiplexer multiplexer_16 (.sel(not_23_out), .in_0(Flag_v_Bus), .in_1(multiplexer_13_out), .out(multiplexer_16_out));
  or or_7 (or_7_out, LD_Rflags_Bus, LD_RFlags);
  not not_23 (not_23_out, LD_Rflags_Bus);
  nor nor_2 (nor_2_out, not_18_out, not_19_out);
  Demultiplexer #(.Selector_Bits(3)) demultiplexer_7 (
    .sel(MAR_q[26:24]), .in(decoder_1_out_1), .out_0(CS_UROM), .out_1(CS_URAM), .out_2(CS_UStack));  // open: out_3, out_4, out_5, out_6, out_7
  Comparator #(.Bits(32)) comparator_6 (
    .a(Gr_Conx_out), .b(register_4_q), .eq(comparator_6_eq), .lt(comparator_6_lt));  // open: gt
  and and_24 (and_24_out, d_ff_as_1_q[0], comparator_6_lt);
  Comparator #(.Bits(32)) comparator_7 (
    .a(Gr_Cony_out), .b(register_5_q), .eq(comparator_7_eq), .lt(comparator_7_lt));  // open: gt
  or or_8 (or_8_out, LD_Rflags_Bus, LD_RFlags);
  or or_9 (or_9_out, LD_Rflags_Bus, LD_RFlags);
  or or_10 (or_10_out, LD_Rflags_Bus, LD_RFlags);
  Register register_10 (.D(multiplexer_16_out), .C(clock_t), .en(or_7_out), .Q(Flag_v));
  JK_FF_AS jk_ff_as_2 (.Set(and_23_out), .J(1'b0), .C(clock_t), .K(OE_INT_REQ), .Clr(1'b0), .Q(AV_MEMERR));  // open: nQ
  CounterPreset #(.Bits(32)) Gr_Conx (
    .en(and_24_out), .C(clock_t), .dir(1'b0), .in({32{1'b0}}), .ld(1'b0), .clr(comparator_6_eq),
    .out(Gr_Conx_out));  // open: ovf
  CounterPreset #(.Bits(32)) Gr_Cony (
    .en(comparator_6_eq), .C(clock_t), .dir(1'b0), .in({32{1'b0}}), .ld(1'b0), .clr(comparator_7_eq),
    .out(Gr_Cony_out));  // open: ovf
  BitSelector #(.Selector_Bits(6)) bitselector_1 (
    .in({register_7_q, register_6_q}), .sel(add_4_s), .out(bitselector_1_out));
  Register register_11 (.D(multiplexer_14_out), .C(clock_t), .en(or_8_out), .Q(Flag_z));
  Register register_12 (.D(multiplexer_11_out), .C(clock_t), .en(or_9_out), .Q(Flag_c));
  Register register_13 (.D(multiplexer_15_out), .C(clock_t), .en(or_10_out), .Q(Flag_n));
  Demultiplexer #(.Selector_Bits(4)) demultiplexer_8 (
    .sel(MAR_q[3:0]), .in(CS_Gr), .out_0(CS_Grx), .out_1(CS_Gry), .out_2(CS_Grw), .out_3(CS_Grh),
    .out_4(CS_Grcolor), .out_5(CS_Grbgcolor), .out_6(CS_Grdatalow), .out_7(CS_Grdatahigh), .out_8(CS_Grmode),
    .out_9(CS_Grstat));  // open: out_10, out_11, out_12, out_13, out_14, out_15
  Multiplexer #(.Bits(32)) multiplexer_17 (
    .sel(bitselector_1_out), .in_0(register_8_q), .in_1(register_3_q), .out(multiplexer_17_out));
  Add #(.Bits(32)) add_2 (.a(register_1_q), .b(Gr_Conx_out), .c_i(1'b0), .s(add_2_s));  // open: c_o
  Add #(.Bits(32)) add_3 (.a(Gr_Cony_out), .b(register_2_q), .c_i(1'b0), .s(add_3_s));  // open: c_o
  Mul #(.Bits(32)) mul_1 (.a(register_4_q), .b(Gr_Cony_out), .mul(mul_1_mul));
  Comparator #(.Bits(32)) comparator_8 (.a(32'h1), .b(register_9_q), .eq(comparator_8_eq));  // open: gt, lt
  Comparator #(.Bits(32)) comparator_9 (.a(32'h2), .b(register_9_q), .eq(comparator_9_eq));  // open: gt, lt
  Mul #(.Bits(32)) mul_2 (.a(32'ha0), .b(add_3_s), .mul(mul_2_mul));
  Add #(.Bits(32)) add_4 (.a(Gr_Conx_out), .b(mul_1_mul[31:0]), .c_i(1'b0), .s({add_4_s_2, add_4_s}));  // open: c_o
  Add #(.Bits(32)) add_5 (.a(add_2_s), .b(mul_2_mul[31:0]), .c_i(1'b0), .s(add_5_s));  // open: c_o
  and and_25 (and_25_out, and_24_out, comparator_7_lt);
  Multiplexer multiplexer_18 (.sel(comparator_9_eq), .in_0(and_25_out), .in_1(and_26_out), .out(multiplexer_18_out));
  and and_26 (and_26_out, and_25_out, bitselector_1_out);
  GraphicCard #(.Bits(32)) Gr (.A(add_5_s[14:0]), .str(multiplexer_18_out), .C(clock_t), .ld(1'b0), .B(1'b0), .D(Gr_d));
  Multiplexer #(.Selector_Bits(3), .Bits(32)) multiplexer_19 (
    .sel(priorityencoder_1_num), .in_0(32'h3000003), .in_1(32'h3000002), .in_2(32'h3000001),
    .in_3(32'h3000000), .in_4(32'h3000007), .in_5(32'h3000006), .in_6(32'h3000004), .in_7(32'h3000005),
    .out(INT_ADDR));
  PriorityEncoder #(.Selector_Bits(3)) priorityencoder_1 (
    .in0(1'b0), .in1(AV_Telnet), .in2(AV_Keyboard), .in3(1'b0), .in4(AV_Tick), .in5(1'b0), .in6(AV_MEMERR),
    .in7(AV_IInstERR), .num(priorityencoder_1_num), .any(INT_REQ));
  Multiplexer #(.Bits(32)) multiplexer_20 (
    .sel(comparator_8_eq), .in_0(register_3_q), .in_1(multiplexer_17_out), .out(Gr_d));
  or or_11 (or_11_out, WE, OE);
  or or_12 (or_12_out, WE, OE);
  or or_13 (or_13_out, WE, OE);
  and and_27 (and_27_out, CS_KeyBoard, OE);
  and and_28 (and_28_out, CS_Terminal, WE);
  and and_29 (and_29_out, CS_Telnet, WE);
  and and_30 (and_30_out, CS_Telnet, OE);
  and and_31 (and_31_out, WE, CS_MIDI);
  or or_14 (or_14_out, WE, OE);
  or or_15 (or_15_out, WE, OE);
  EEPROM #(.AddrBits(24), .Bits(32)) ROM (.A(MAR_q[23:0]), .CS(CS_ROM), .WE(1'b0), .OE(OE), .D(driver_12_out));
  RAMSinglePortSel #(.AddrBits(24), .Bits(32)) RAM (
    .A(MAR_q[23:0]), .CS(delay_2_out), .WE(WE), .OE(OE), .D(driver_12_out));
  Delay delay_2 (.in(and_32_out), .out(delay_2_out));
  and and_32 (and_32_out, CS_RAM, or_11_out);
  RAMSinglePortSel #(.AddrBits(24), .Bits(32)) Stack (
    .A(MAR_q[23:0]), .CS(delay_3_out), .WE(WE), .OE(OE), .D(driver_12_out));
  Delay delay_3 (.in(and_33_out), .out(delay_3_out));
  and and_33 (and_33_out, CS_Stack, or_12_out);
  RAMSinglePortSel #(.AddrBits(24), .Bits(32)) IVT (
    .A(MAR_q[23:0]), .CS(delay_4_out), .WE(WE), .OE(OE), .D(driver_12_out));
  Delay delay_4 (.in(and_34_out), .out(delay_4_out));
  and and_34 (and_34_out, CS_IVT, or_13_out);
  Keyboard keyboard_1 (.C(clock_t), .en(and_27_out), .D(keyboard_1_d), .av(AV_Keyboard));
  Terminal terminal_1 (.D(driver_12_out[15:0]), .C(clock_t), .en(and_28_out));
  Telnet #(.port(8081)) telnet_1 (
    .in(driver_12_out[7:0]), .C(clock_t), .wr(and_29_out), .rd(and_30_out), .out(telnet_1_out), .av(AV_Telnet));
  and and_35 (and_35_out, CS_Tick, OE);
  Counter #(.Bits(14)) Tick (.en(1'b1), .C(clock_t), .clr(CS_Tick), .ovf(Tick_ovf));  // open: out
  Counter #(.Bits(32)) Timer (.en(not_24_out), .C(clock_1000hz), .clr(1'b0), .out(Timer_out));  // open: ovf
  not not_24 (not_24_out, HALT);
  // MIDI #(.midiProgChange("true"), .midiChannel(16)) MIDI: pin names not known; wires that end beside it: driver_12_out[6:0], driver_12_out[7], driver_12_out[8], and_31_out, clock_t
  EEPROM #(.AddrBits(24), .Bits(32)) UROM (.A(MAR_q[23:0]), .CS(CS_UROM), .WE(1'b0), .OE(OE), .D(driver_12_out));
  RAMSinglePortSel #(.AddrBits(24), .Bits(32)) URAM (
    .A(MAR_q[23:0]), .CS(delay_5_out), .WE(WE), .OE(OE), .D(driver_12_out));
  Delay delay_5 (.in(and_36_out), .out(delay_5_out));
  and and_36 (and_36_out, CS_URAM, or_14_out);
  RAMSinglePortSel #(.AddrBits(24), .Bits(32)) UStack (
    .A(MAR_q[23:0]), .CS(delay_6_out), .WE(WE), .OE(OE), .D(driver_12_out));
  Delay delay_6 (.in(and_37_out), .out(delay_6_out));
  and and_37 (and_37_out, CS_UStack, or_15_out);
  assign driver_12_out = and_38_out ? {{16{1'b0}}, keyboard_1_d} : 32'bz;  // Driver driver_14
  RS_FF_AS rs_ff_as_1 (.S(Tick_ovf), .R(CS_Tick), .Q(AV_Tick));  // open: nQ
  and and_38 (and_38_out, CS_KeyBoard, OE);
  and and_39 (and_39_out, CS_Telnet, OE);
  assign driver_12_out = and_39_out ? {{24{1'b0}}, telnet_1_out} : 32'bz;  // Driver driver_15
  assign driver_12_out = and_35_out ? 32'h1 : 32'bz;  // Driver driver_16
  assign driver_12_out = CS_Timer ? Timer_out : 32'bz;  // Driver driver_17

  // Notes on the sheet:
  //   Clock: Hz: 6553600
  //   clock_1000hz: Hz: 1000
  //   CU
  //   contents of CU_INT (hex, n*v repeats v):
  //   3c280080,43c000000,3c002020,3e010002,3c002020,3c004080,3e010002
  //   ,83c000020,3d000040,113c008010
  //   contents of CU_U (hex, n*v repeats v):
  //   3c004020,3d800040,3c008100,13c000000,12*3c000000,3c004020,3d800040
  //   ,3c008100,13c000000,12*3c000000,3c004020,3d800040,3c008100,13c000000
  //   ,12*3c000000,3c004020,3d800040,3c008100,13c000000,12*3c000000
  //   ,3c004020,3d800040,3c008100,13c000000,12*3c000000,3c004020,3d800040
  //   ,3c008100,13c000000,12*3c000000,3c004020,3d800040,3c008100,13c000000
  //   ,12*3c000000,3c004020,3d800040,3c008100,13c000000,12*3c000000
  //   ,3c004020,3d800040,3c008100,13c000000,12*3c000000,3c004020,3d800040
  //   ,3c008100,13c000000,12*3c000000,3c004020,3d800040,3c008100,13c000000
  //   ,12*3c000000,3c004020,3d800040,3c008100,13c000000,12*3c000000
  //   ,3c004020,3d800040,3c008100,13c000000,12*3c000000,3c004020,3d800040
  //   ,3c008100,13c000000,12*3c000000,3c004020,3d800040,3c008100,13c000000
  //   ,12*3c000000,3c004020,3d800040,3c008100,13c000000,12*3c000000
  //   ,3c004020,3d800040,3c008100,13c020200,12*3c000000,3c004020,3d800040
  //   ,3c008100,3c040020,3d000040,13c008200,10*3c000000,3c004020,3d800040
  //   ,3c008100,3c040020,3c020080,13e010000,10*3c000000,3c004020,3d800040
  //   ,3c008100,3c004020,3d800040,3c008020,3d000040,13c008200,8*3c000000
  //   ,3c004020,3d800040,3c008100,3c004020,3d800040,3c008020,3c020080
  //   ,13e010000,8*3c000000,3c004020,3d800040,3c008100,3c804020,3d000040
  //   ,13c008200,10*3c000000,3c004020,3d800040,3c008100,3c804020,3d000040
  //   ,13c008200,10*3c000000,3c004020,3d800040,3c008100,100020,3d000040
  //   ,13c008200,10*3c000000,3c004020,3d800040,3c008100,13c000000,12*3c000000
  //   ,3c004020,3d800040,3c008100,13c000000,12*3c000000,3c004020,3d800040
  //   ,3c008100,13c000000,12*3c000000,3c004020,3d800040,3c008100,13c000000
  //   ,12*3c000000,3c004020,3d800040,3c008100,13c000000,12*3c000000
  //   ,3c004020,3d800040,3c008100,13c000000,12*3c000000,3c004020,3d800040
  //   ,3c008100,13c000000,12*3c000000,3c004020,3d800040,3c008100,13c000000
  //   ,12*3c000000,3c004020,3d800040,3c008100,100100600,12*3c000000
  //   ,3c004020,3d800040,3c008100,104100600,12*3c000000,3c004020,3d800040
  //   ,3c008100,130100200,12*3c000000,3c004020,3d800040,3c008100,134100200
  //   ,12*3c000000,3c004020,3d800040,3c008100,108100600,12*3c000000
  //   ,3c004020,3d800040,3c008100,10c100600,12*3c000000,3c004020,3d800040
  //   ,3c008100,138100600,12*3c000000,3c004020,3d800040,3c008100,110100600
  //   ,12*3c000000,3c004020,3d800040,3c008100,114100600,12*3c000000
  //   ,3c004020,3d800040,3c008100,118100600,12*3c000000,3c004020,3d800040
  //   ,3c008100,11c100600,12*3c000000,3c004020,3d800040,3c008100,120100600
  //   ,12*3c000000,3c004020,3d800040,3c008100,124100600,12*3c000000
  //   ,3c004020,3d800040,3c008100,128100600,12*3c000000,3c004020,3d800040
  //   ,3c008100,12c100600,12*3c000000,3c004020,3d800040,3c008100,104000400
  //   ,12*3c000000,3c004020,3d800040,3c008100,3c004020,3d800040,13c008010
  //   ,10*3c000000,3c004020,3d800040,3c008100,80000000,3c004020,3d800040
  //   ,13c008010,9*3c000000,3c004020,3d800040,3c008100,13c020010,12*3c000000
  //   ,3c004020,3d800040,3c008100,80000000,13c020010,11*3c000000,3c004020
  //   ,3d800040,3c008100,3c804020,3d000040,3c002020,3c004080,3e010002
  //   ,13c008010,7*3c000000,3c004020,3d800040,3c008100,80000000,3c804020
  //   ,3d000040,3c002020,3c004080,3e010002,13c008010,6*3c000000,3c004020
  //   ,3d800040,3c008100,3c000001,3c002020,3d000040,13c008010,9*3c000000
  //   ,3c004020,3d800040,3c008100,3ca04020,3d000040,3c080080,43c000000
  //   ,3c002020,3e010002,3c002020,3c004080,3e010002,13c008010,3c000000,3c000000,3c000000
  //   ,3c004020,3d800040,3c008100,bc000000,3ca04020,3d000040,3c080080
  //   ,43c000000,3c002020,3e010002,3c002020,3c004080,3e010002,13c008010
  //   ,3c000000,3c000000,3c004020,3d800040,3c008100,93c000000,12*3c000000
  //   ,3c004020,3d800040,3c008100,93c000000,12*3c000000,3c004020,3d800040
  //   ,3c008100,93c000000,12*3c000000,3c004020,3d800040,3c008100,13c000000
  //   ,12*3c000000,3c004020,3d800040,3c008100,13c000000,12*3c000000
  //   ,3c004020,3d800040,3c008100,13c000000,12*3c000000,3c004020,3d800040
  //   ,3c008100,13c000000,12*3c000000,3c004020,3d800040,3c008100,3c002020
  //   ,3c020080,13e010002,10*3c000000,3c004020,3d800040,3c008100,3c000001
  //   ,3c002020,3d000040,13c008200,9*3c000000,3c004020,3d800040,3c008100
  //   ,13c020008,12*3c000000,3c004020,3d800040,3c008100,13c002200,12*3c000000
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  //   contents of CU_K (hex, n*v repeats v):
  //   3c004020,3d800040,3c008100,13c000000,12*3c000000,3c004020,3d800040
  //   ,3c008100,13c000000,12*3c000000,3c004020,3d800040,3c008100,13c000000
  //   ,12*3c000000,3c004020,3d800040,3c008100,13c000000,12*3c000000
  //   ,3c004020,3d800040,3c008100,13c000000,12*3c000000,3c004020,3d800040
  //   ,3c008100,13c000000,12*3c000000,3c004020,3d800040,3c008100,13c000000
  //   ,12*3c000000,3c004020,3d800040,3c008100,13c000000,12*3c000000
  //   ,3c004020,3d800040,3c008100,13c000000,12*3c000000,3c004020,3d800040
  //   ,3c008100,13c000000,12*3c000000,3c004020,3d800040,3c008100,13c000000
  //   ,12*3c000000,3c004020,3d800040,3c008100,13c000000,12*3c000000
  //   ,3c004020,3d800040,3c008100,13c000000,12*3c000000,3c004020,3d800040
  //   ,3c008100,13c000000,12*3c000000,3c004020,3d800040,3c008100,13c000000
  //   ,12*3c000000,3c004020,3d800040,3c008100,13c000000,12*3c000000
  //   ,3c004020,3d800040,3c008100,13c020200,12*3c000000,3c004020,3d800040
  //   ,3c008100,3c040020,3d000040,13c008200,10*3c000000,3c004020,3d800040
  //   ,3c008100,3c040020,3c020080,13e010000,10*3c000000,3c004020,3d800040
  //   ,3c008100,3c004020,3d800040,3c008020,3d000040,13c008200,8*3c000000
  //   ,3c004020,3d800040,3c008100,3c004020,3d800040,3c008020,3c020080
  //   ,13e010000,8*3c000000,3c004020,3d800040,3c008100,3c804020,3d000040
  //   ,13c008200,10*3c000000,3c004020,3d800040,3c008100,3c804020,3d000040
  //   ,13c008200,10*3c000000,3c004020,3d800040,3c008100,100020,3d000040
  //   ,13c008200,10*3c000000,3c004020,3d800040,3c008100,13c000000,12*3c000000
  //   ,3c004020,3d800040,3c008100,13c000000,12*3c000000,3c004020,3d800040
  //   ,3c008100,13c000000,12*3c000000,3c004020,3d800040,3c008100,13c000000
  //   ,12*3c000000,3c004020,3d800040,3c008100,13c000000,12*3c000000
  //   ,3c004020,3d800040,3c008100,13c000000,12*3c000000,3c004020,3d800040
  //   ,3c008100,13c000000,12*3c000000,3c004020,3d800040,3c008100,13c000000
  //   ,12*3c000000,3c004020,3d800040,3c008100,100100600,12*3c000000
  //   ,3c004020,3d800040,3c008100,104100600,12*3c000000,3c004020,3d800040
  //   ,3c008100,130100200,12*3c000000,3c004020,3d800040,3c008100,134100200
  //   ,12*3c000000,3c004020,3d800040,3c008100,108100600,12*3c000000
  //   ,3c004020,3d800040,3c008100,10c100600,12*3c000000,3c004020,3d800040
  //   ,3c008100,138100600,12*3c000000,3c004020,3d800040,3c008100,110100600
  //   ,12*3c000000,3c004020,3d800040,3c008100,114100600,12*3c000000
  //   ,3c004020,3d800040,3c008100,118100600,12*3c000000,3c004020,3d800040
  //   ,3c008100,11c100600,12*3c000000,3c004020,3d800040,3c008100,120100600
  //   ,12*3c000000,3c004020,3d800040,3c008100,124100600,12*3c000000
  //   ,3c004020,3d800040,3c008100,128100600,12*3c000000,3c004020,3d800040
  //   ,3c008100,12c100600,12*3c000000,3c004020,3d800040,3c008100,104000400
  //   ,12*3c000000,3c004020,3d800040,3c008100,3c004020,3d800040,13c008010
  //   ,10*3c000000,3c004020,3d800040,3c008100,80000000,3c004020,3d800040
  //   ,13c008010,9*3c000000,3c004020,3d800040,3c008100,13c020010,12*3c000000
  //   ,3c004020,3d800040,3c008100,80000000,13c020010,11*3c000000,3c004020
  //   ,3d800040,3c008100,3c804020,3d000040,3c002020,3c004080,3e010002
  //   ,13c008010,7*3c000000,3c004020,3d800040,3c008100,80000000,3c804020
  //   ,3d000040,3c002020,3c004080,3e010002,13c008010,6*3c000000,3c004020
  //   ,3d800040,3c008100,3c000001,3c002020,3d000040,13c008010,9*3c000000
  //   ,3c004020,3d800040,3c008100,3ca04020,3d000040,3c080080,43c000000
  //   ,3c002020,3e010002,3c002020,3c004080,3e010002,13c008010,3c000000,3c000000,3c000000
  //   ,3c004020,3d800040,3c008100,bc000000,3ca04020,3d000040,3c080080
  //   ,43c000000,3c002020,3e010002,3c002020,3c004080,3e010002,13c008010
  //   ,3c000000,3c000000,3c004020,3d800040,3c008100,3c400001,3c002020
  //   ,3d000040,3c008011,3c002020,3d000040,13c008800,6*3c000000,3c004020
  //   ,3d800040,3c008100,13c400000,12*3c000000,3c004020,3d800040,3c008100
  //   ,13c200000,12*3c000000,3c004020,3d800040,3c008100,13c000000,12*3c000000
  //   ,3c004020,3d800040,3c008100,13c000000,12*3c000000,3c004020,3d800040
  //   ,3c008100,13c000000,12*3c000000,3c004020,3d800040,3c008100,13c000000
  //   ,12*3c000000,3c004020,3d800040,3c008100,3c002020,3c020080,13e010002
  //   ,10*3c000000,3c004020,3d800040,3c008100,3c000001,3c002020,3d000040
  //   ,13c008200,9*3c000000,3c004020,3d800040,3c008100,13c020008,12*3c000000
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  //   ALU
  //   MPU
  //   GPU
  //   contents of ROM (hex, n*v repeats v):
  //   30,88c,46,45,e43,f15,6,efe20,e0042,249,f15,1,2f220,2012,49,f15
  //   ,2,f020,10012,49,f15,3,f020,115,ff,10012,2111,11,10128,12012,49
  //   ,f15,4,f020,115,1fffb7c,10012,11,115,13,1020,11,115,0,102f,500031
  //   ,3e,30,31,49,115,0,10012,49,f15,5,f020,115,1,10012,30,9f,49,f15
  //   ,4,f020,11,115,15,1020,11,115,0,102f,500031,62,30,4e,49,f15,1
  //   ,f020,11,34,a4,49,115,0,10012,49,f15,5,f020,115,1,10012,30,9f
  //   ,15,1fffe92,111,215,1,12120,215,ffff,12128,10012,11,115,0,102f
  //   ,500031,7b,30,74,15,1fffe92,115,1,10012,30,7b,15,1fffe92,11,115
  //   ,1fffe93,1111,1024,149,f15,1,1f120,1111,102a,115,a5000000,102a
  //   ,34,ba,49,f15,2,f020,11,34,161,149,1012,49,f15,5,f020,115,1,10012
  //   ,30,9f,49,11,44,47,36,115,1fffe70,1211,315,1,23220,315,1f,23228
  //   ,315,1fffe71,3311,2302f,200031,b9,1311,a15,1fffe72,3a320,3012
  //   ,21012,36,46,45,e43,f15,5,efe20,e0042,e49,4e012,149,f15,1,1f120
  //   ,1012,449,f15,2,4f420,15,1fffb7c,4012,4011,115,5d,1020,11,34,2609
  //   ,149,f15,3,1f120,1012,1011,4111,215,5c,12120,1111,102f,500031
  //   ,fa,30,e6,49,f15,2,f020,11,115,5e,1020,111,215,1,12120,10012,49
  //   ,f15,4,f020,20012,30,15a,49,f15,1,f020,11,149,f15,2,1f120,1211
  //   ,315,5d,23a20,aa11,2a220,a15,1c,2a220,2012,49,f15,3,f020,11,1211
  //   ,23220,2012,1011,115,5f,1020,11,115,0,102f,200031,144,30,121,49
  //   ,f15,2,f020,111,215,5f,12120,215,0,21012,111,315,65,13120,21012
  //   ,111,315,60,13120,21012,111,315,63,13120,21012,11,115,62,1020
  //   ,115,1,10012,30,151,49,f15,2,f020,11,115,60,1020,115,1,10012,30
  //   ,151,49,f15,4,f020,115,0,10012,30,15a,30,15c,e49,e411,44,47,36
  //   ,46,45,e43,f15,6,efe20,e0042,149,f15,1,1f120,1012,49,f15,2,f020
  //   ,115,1fffb7c,10012,15,1fffe94,11,115,1,102f,500031,185,30,17e
  //   ,49,f15,1,f020,11,30,190,49,f15,2,f020,11,115,12,1020,11,30,190
  //   ,149,f15,3,1f120,1012,1011,34,769,149,f15,4,1f120,1012,1011,115
  //   ,0,102f,500031,1b2,30,1a5,49,115,0,10012,49,f15,5,f020,115,1,10012
  //   ,30,1e7,15,1fffe94,11,115,1,102f,500031,1cc,30,1bc,49,f15,4,f020
  //   ,11,149,1012,49,f15,5,f020,115,1,10012,30,1e7,49,f15,4,f020,11
  //   ,149,f15,2,1f120,1111,215,12,12120,1012,49,115,0,10012,49,f15
  //   ,5,f020,115,1,10012,30,1e7,49,11,44,47,36,46,45,e43,f15,7,efe20
  //   ,e0042,249,f15,1,2f220,2012,49,f15,2,f020,10012,49,f15,3,f020
  //   ,115,ff,10012,2111,11,10128,12012,49,f15,4,f020,115,1fffb7c,10012
  //   ,11,115,13,1020,11,115,0,102f,500031,228,30,21b,49,115,0,10012
  //   ,49,f15,5,f020,115,1,10012,30,2ad,49,f15,4,f020,11,115,1a,1020
  //   ,11,115,0,102f,500031,270,30,238,15,1fffad3,11,115,1,1020,115
  //   ,3f,1028,149,f15,6,1f120,1012,1011,115,1fffad4,1111,102f,200031
  //   ,263,30,24f,49,f15,1,f020,11,115,1fffad3,1211,315,1fffad5,23220
  //   ,2012,49,f15,6,f020,11,1012,30,263,49,115,0,10012,49,f15,5,f020
  //   ,115,1,10012,30,2ad,15,1fffb15,111,215,1,12120,215,ffff,12128
  //   ,10012,11,115,0,102f,500031,289,30,282,15,1fffb15,115,1,10012
  //   ,30,289,15,1fffb15,11,115,1fffe93,1111,1024,149,f15,1,1f120,1111
  //   ,102a,115,a6000000,102a,34,ba,49,f15,2,f020,11,34,161,149,1012
  //   ,49,f15,5,f020,115,1,10012,30,2ad,49,11,44,47,36,46,45,e43,f15
  //   ,4,efe20,e0042,49,115,1fffb7c,10012,149,f15,1,1f120,215,2010000
  //   ,21012,211,315,11,23220,2211,1311,23012,11,215,10,2020,11,1111
  //   ,215,1,12120,1012,49,f15,2,f020,115,0,10012,30,2de,49,f15,2,f020
  //   ,11,115,10,102f,100031,2ec,30,2ea,30,30d,49,11,149,f15,2,1f120
  //   ,1211,2020,11,249,f15,1,2f220,2211,1111,21120,215,2,12120,1012
  //   ,30,302,49,f15,2,f020,111,215,1,12120,10012,30,2de,49,f15,1,f020
  //   ,11,115,12,1020,249,f15,3,2f220,2012,49,311,a15,18,3a320,a15,0
  //   ,a3012,311,b15,17,3b320,a3012,2311,b11,b1120,31012,111,315,63
  //   ,13120,315,1,31012,11,115,62,1020,a0012,2011,44,47,36,46,45,e43
  //   ,f15,6,efe20,e0042,149,f15,1,1f120,1012,34,494,49,f15,2,f020,115
  //   ,1fffb16,10012,49,f15,3,f020,115,1fffb7c,10012,11,115,13,1020
  //   ,11,115,0,102f,200031,3ac,30,363,49,f15,3,f020,11,115,5f,1020
  //   ,11,115,0,102f,200031,3ac,30,373,49,f15,3,f020,11,115,65,1020
  //   ,11,115,0,102f,200031,3ac,30,383,15,8000000,11,149,f15,3,1f120
  //   ,1211,315,64,23220,2211,2021,1111,215,65,12120,1111,102f,100031
  //   ,3ac,30,39a,49,f15,3,f020,111,215,5f,12120,215,0,21012,11,115
  //   ,65,1020,20012,30,3ac,15,1fffe94,11,115,0,102f,500031,465,30,3b6
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  //   contents of UROM (hex, n*v repeats v):
  //   30,80000009,15,7,37,25e1,0,30,6,e15,82000000,e0042,e0048,e43,f15
  //   ,4a,efe20,e0042,e49,f15,5,efe20,4e012,e49,f15,4,efe20,5e012,e49
  //   ,f15,3,efe20,6e012,e49,f15,2,efe20,7e012,e49,f15,1,efe20,8e012
  //   ,e49,9e012,15,81ffffe1,115,4b,e49,f15,2d,efe20,1e012,10012,115
  //   ,81ffffe2,b15,65,b1012,115,81ffffe3,215,79,e49,f15,35,efe20,2e012
  //   ,21012,115,81ffffe4,215,62,21012,20310,e49,f15,39,efe20,3e012
  //   ,115,81ffffe5,15,6f,1012,510,e49,f15,1e,efe20,5e012,115,81ffffe6
  //   ,c15,61,c1012,115,81ffffe7,215,72,21012,115,81ffffe8,a15,64,a1012
  //   ,a0610,e49,f15,20,efe20,6e012,115,81ffffe9,415,20,41012,115,81ffffea
  //   ,d15,73,d1012,115,81ffffeb,15,75,e49,f15,1b,efe20,e012,1012,115
  //   ,81ffffec,31012,115,81ffffed,d1012,115,81ffffee,a15,63,a1012,a0310
  //   ,e49,f15,1c,efe20,3e012,115,81ffffef,21012,20010,115,81fffff0
  //   ,215,69,21012,115,81fffff1,a15,70,e49,f15,21,efe20,ae012,a1012
  //   ,115,81fffff2,715,74,71012,115,81fffff3,21012,e49,f15,3e,efe20
  //   ,2e012,115,81fffff4,51012,115,81fffff5,515,6e,51012,115,81fffff6
  //   ,41012,115,81fffff7,a15,66,e49,f15,1f,efe20,ae012,a1012,115,81fffff8
  //   ,c1012,115,81fffff9,21012,115,81fffffa,215,6c,e49,f15,26,efe20
  //   ,2e012,21012,115,81fffffb,b1012,115,81fffffc,61012,115,81fffffd
  //   ,215,2e,e49,f15,29,efe20,2e012,21012,115,81fffffe,a15,a,a1012
  //   ,e49,f15,1d,efe20,ae012,115,81ffffff,215,0,e49,f15,28,efe20,2e012
  //   ,21012,115,81ffff47,215,53,21012,20610,115,81ffff48,31012,115
  //   ,81ffff49,1012,115,81ffff4a,b1012,115,81ffff4b,b1012,115,81ffff4c
  //   ,e49,f15,1a,efe20,5e012,51012,115,81ffff4d,41012,115,81ffff4e
  //   ,61012,115,81ffff4f,51012,115,81ffff50,c1012,115,81ffff51,215
  //   ,6b,e49,f15,2f,efe20,2e012,21012,115,81ffff52,b1012,115,81ffff53
  //   ,a1012,115,81ffff54,61012,60a10,e49,f15,32,efe20,ae012,915,81ffff55
  //   ,815,50,89012,915,81ffff56,115,41,19012,e49,f15,37,efe20,1e012
  //   ,915,81ffff57,615,43,e49,f15,25,efe20,6e012,69012,915,81ffff58
  //   ,215,45,e49,f15,2e,efe20,2e012,29012,915,81ffff59,49012,915,81ffff5a
  //   ,d9012,915,81ffff5b,e49,f15,22,efe20,7e012,79012,915,81ffff5c
  //   ,c9012,915,81ffff5d,9012,510,e49,f15,2b,efe20,5e012,915,81ffff5e
  //   ,79012,915,81ffff5f,49012,915,81ffff60,15,2f,e49,f15,3c,efe20
  //   ,e012,9012,915,81ffff61,49012,915,81ffff62,e49,f15,21,ef017,9012
  //   ,915,81ffff63,c9012,915,81ffff64,e49,f15,1b,ef317,39012,915,81ffff65
  //   ,d9012,915,81ffff66,b9012,915,81ffff67,49012,915,81ffff68,49012
  //   ,915,81ffff69,49012,915,81ffff6a,615,57,e49,f15,36,efe20,6e012
  //   ,69012,915,81ffff6b,19012,915,81ffff6c,a9012,915,81ffff6d,715
  //   ,44,e49,f15,34,efe20,7e012,79012,915,81ffff6e,49012,915,81ffff6f
  //   ,215,6d,29012,915,81ffff70,e49,f15,1e,ef617,69012,915,81ffff71
  //   ,115,76,e49,f15,30,efe20,1e012,19012,915,81ffff72,b9012,915,81ffff73
  //   ,e49,f15,1d,ef117,19012,915,81ffff74,89012,115,81ffff75,41012
  //   ,115,81ffff76,1012,115,81ffff77,c1012,115,81ffff78,30710,71012
  //   ,115,81ffff79,d1012,115,81ffff7a,b1012,115,81ffff7b,41012,115
  //   ,81ffff7c,e49,f15,3c,ef317,31012,115,81ffff7d,41012,115,81ffff7e
  //   ,51012,115,81ffff7f,b1012,115,81ffff80,d1012,115,81ffff81,71012
  //   ,70010,115,81ffff82,e49,f15,27,efe20,2e012,21012,115,81ffff83
  //   ,b1012,115,81ffff84,41012,115,81ffff85,41012,115,81ffff86,41012
  //   ,115,81ffff87,41012,115,81ffff88,41012,115,81ffff89,715,4d,e49
  //   ,f15,41,efe20,7e012,71012,115,81ffff8a,41012,115,81ffff8b,21012
  //   ,115,81ffff8c,1012,115,81ffff8d,d1012,115,81ffff8e,e49,f15,3e
  //   ,ef217,21012,115,81ffff8f,e49,f15,1c,efa17,a1012,115,81ffff90
  //   ,41012,915,81ffff91,115,2b,19012,915,81ffff92,49012,915,81ffff93
  //   ,d9012,915,81ffff94,60510,59012,915,81ffff95,9012,915,81ffff96
  //   ,e49,f15,1a,ef017,9012,915,81ffff97,e49,f15,20,ef617,69012,915
  //   ,81ffff98,49012,915,81ffff99,59012,915,81ffff9a,9012,915,81ffff9b
  //   ,30a10,a9012,915,81ffff9c,59012,915,81ffff9d,e49,f15,1f,ef717
  //   ,79012,915,81ffff9e,79012,70510,915,81ffff9f,e49,f15,1d,ef017
  //   ,9012,915,81ffffa0,19012,115,81ffffa1,a1012,115,81ffffa2,915,2d
  //   ,91012,115,81ffffa3,41012,115,81ffffa4,d1012,115,81ffffa5,e49
  //   ,f15,21,ef017,1012,115,81ffffa6,b1012,115,81ffffa7,b1012,b0010
  //   ,115,81ffffa8,61012,60810,115,81ffffa9,41012,115,81ffffaa,b15
  //   ,28,e49,f15,40,efe20,be012,b1012,115,81ffffab,b15,31,e49,f15,44
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endmodule
